// Logisim project Final Project - Pipeline.circ as structural Verilog: 20 circuits, main circuit Register File
module Register_File (
  input  [31:0] Write_data,
  input  [4:0] Read_Register_2,
  input  [4:0] Read_Register_1,
  input  [4:0] Write_Register,
  input  RegWrite,
  input  Clock,
  output [31:0] R15,
  output [31:0] R16,
  output [31:0] R14,
  output [31:0] R17,
  output [31:0] R13,
  output [31:0] R18,
  output [31:0] R12,
  output [31:0] R19,
  output [31:0] R11,
  output [31:0] R20,
  output [31:0] R10,
  output [31:0] R21,
  output [31:0] R9,
  output [31:0] R22,
  output [31:0] R8,
  output [31:0] R23,
  output [31:0] R7,
  output [31:0] R24,
  output [31:0] R6,
  output [31:0] R25,
  output [31:0] R5,
  output [31:0] R26,
  output [31:0] R4,
  output [31:0] R27,
  output [31:0] R3,
  output [31:0] R28,
  output [31:0] R2,
  output [31:0] R29,
  output [31:0] R1,
  output [31:0] R30,
  output [31:0] R31,
  output [31:0] Read_Data_1,
  output [31:0] Read_Data_2
);

  wire and_2_out, and_3_out, and_4_out, and_5_out, and_6_out, and_7_out, and_8_out, and_9_out, and_10_out,
       and_11_out, and_12_out, and_13_out, and_14_out, and_15_out, and_16_out, and_17_out, and_18_out,
       and_19_out, and_20_out, and_21_out, and_22_out, and_23_out, and_24_out, and_25_out, and_26_out,
       and_27_out, and_28_out, and_29_out, and_30_out, and_31_out, and_32_out, decoder_1_out0,
       decoder_1_out1, decoder_1_out2, decoder_1_out3, decoder_1_out4, decoder_1_out5, decoder_1_out6,
       decoder_1_out7, decoder_1_out8, decoder_1_out9, decoder_1_out10, decoder_1_out11, decoder_1_out12,
       decoder_1_out13, decoder_1_out14, decoder_1_out15, decoder_1_out16, decoder_1_out17, decoder_1_out18,
       decoder_1_out19, decoder_1_out20, decoder_1_out21, decoder_1_out22, decoder_1_out23, decoder_1_out24,
       decoder_1_out25, decoder_1_out26, decoder_1_out27, decoder_1_out28, decoder_1_out29, decoder_1_out30,
       decoder_1_out31;
  wire [31:0] register_1_q;

  Decoder #(.select(5), .enable("false")) decoder_1 (
    .out0(decoder_1_out0), .out1(decoder_1_out1), .out2(decoder_1_out2), .out3(decoder_1_out3),
    .out4(decoder_1_out4), .out5(decoder_1_out5), .out6(decoder_1_out6), .out7(decoder_1_out7),
    .out8(decoder_1_out8), .out9(decoder_1_out9), .out10(decoder_1_out10), .out11(decoder_1_out11),
    .out12(decoder_1_out12), .out13(decoder_1_out13), .out14(decoder_1_out14), .out15(decoder_1_out15),
    .out16(decoder_1_out16), .out17(decoder_1_out17), .out18(decoder_1_out18), .out19(decoder_1_out19),
    .out20(decoder_1_out20), .out21(decoder_1_out21), .out22(decoder_1_out22), .out23(decoder_1_out23),
    .out24(decoder_1_out24), .out25(decoder_1_out25), .out26(decoder_1_out26), .out27(decoder_1_out27),
    .out28(decoder_1_out28), .out29(decoder_1_out29), .out30(decoder_1_out30), .out31(decoder_1_out31),
    .sel(Write_Register));
  // AND_Gate and_1 has open pins: in0=decoder_1_out0, in1=RegWrite, out=open
  and and_2 (and_2_out, decoder_1_out1, RegWrite);
  and and_3 (and_3_out, decoder_1_out2, RegWrite);
  and and_4 (and_4_out, decoder_1_out3, RegWrite);
  and and_5 (and_5_out, decoder_1_out4, RegWrite);
  and and_6 (and_6_out, decoder_1_out5, RegWrite);
  and and_7 (and_7_out, decoder_1_out6, RegWrite);
  and and_8 (and_8_out, decoder_1_out7, RegWrite);
  and and_9 (and_9_out, decoder_1_out8, RegWrite);
  and and_10 (and_10_out, decoder_1_out9, RegWrite);
  and and_11 (and_11_out, decoder_1_out10, RegWrite);
  and and_12 (and_12_out, decoder_1_out11, RegWrite);
  and and_13 (and_13_out, decoder_1_out12, RegWrite);
  and and_14 (and_14_out, decoder_1_out13, RegWrite);
  and and_15 (and_15_out, decoder_1_out14, RegWrite);
  and and_16 (and_16_out, decoder_1_out15, RegWrite);
  and and_17 (and_17_out, decoder_1_out16, RegWrite);
  and and_18 (and_18_out, decoder_1_out17, RegWrite);
  and and_19 (and_19_out, decoder_1_out18, RegWrite);
  and and_20 (and_20_out, decoder_1_out19, RegWrite);
  and and_21 (and_21_out, decoder_1_out20, RegWrite);
  and and_22 (and_22_out, decoder_1_out21, RegWrite);
  and and_23 (and_23_out, decoder_1_out22, RegWrite);
  and and_24 (and_24_out, decoder_1_out23, RegWrite);
  and and_25 (and_25_out, decoder_1_out24, RegWrite);
  and and_26 (and_26_out, decoder_1_out25, RegWrite);
  and and_27 (and_27_out, decoder_1_out26, RegWrite);
  and and_28 (and_28_out, decoder_1_out27, RegWrite);
  and and_29 (and_29_out, decoder_1_out28, RegWrite);
  and and_30 (and_30_out, decoder_1_out29, RegWrite);
  and and_31 (and_31_out, decoder_1_out30, RegWrite);
  and and_32 (and_32_out, decoder_1_out31, RegWrite);
  Register #(.width(32), .trigger("falling")) register_1 (
    .D({32{1'b0}}), .Q(register_1_q), .clk(Clock));  // open: en, clr
  Register #(.width(32), .trigger("falling")) register_2 (
    .D(Write_data), .en(and_2_out), .Q(R1), .clk(Clock));  // open: clr
  Register #(.width(32), .trigger("falling")) register_3 (
    .D(Write_data), .en(and_3_out), .Q(R2), .clk(Clock));  // open: clr
  Register #(.width(32), .trigger("falling")) register_4 (
    .D(Write_data), .en(and_4_out), .Q(R3), .clk(Clock));  // open: clr
  Register #(.width(32), .trigger("falling")) register_5 (
    .D(Write_data), .en(and_5_out), .Q(R4), .clk(Clock));  // open: clr
  Register #(.width(32), .trigger("falling")) register_6 (
    .D(Write_data), .en(and_6_out), .Q(R5), .clk(Clock));  // open: clr
  Register #(.width(32), .trigger("falling")) register_7 (
    .D(Write_data), .en(and_7_out), .Q(R6), .clk(Clock));  // open: clr
  Register #(.width(32), .trigger("falling")) register_8 (
    .D(Write_data), .en(and_8_out), .Q(R7), .clk(Clock));  // open: clr
  Register #(.width(32), .trigger("falling")) register_9 (
    .D(Write_data), .en(and_9_out), .Q(R8), .clk(Clock));  // open: clr
  Register #(.width(32), .trigger("falling")) register_10 (
    .D(Write_data), .en(and_10_out), .Q(R9), .clk(Clock));  // open: clr
  Register #(.width(32), .trigger("falling")) register_11 (
    .D(Write_data), .en(and_11_out), .Q(R10), .clk(Clock));  // open: clr
  Register #(.width(32), .trigger("falling")) register_12 (
    .D(Write_data), .en(and_12_out), .Q(R11), .clk(Clock));  // open: clr
  Register #(.width(32), .trigger("falling")) register_13 (
    .D(Write_data), .en(and_13_out), .Q(R12), .clk(Clock));  // open: clr
  Register #(.width(32), .trigger("falling")) register_14 (
    .D(Write_data), .en(and_14_out), .Q(R13), .clk(Clock));  // open: clr
  Register #(.width(32), .trigger("falling")) register_15 (
    .D(Write_data), .en(and_15_out), .Q(R14), .clk(Clock));  // open: clr
  Register #(.width(32), .trigger("falling")) register_16 (
    .D(Write_data), .en(and_16_out), .Q(R15), .clk(Clock));  // open: clr
  Register #(.width(32), .trigger("falling")) register_17 (
    .D(Write_data), .en(and_17_out), .Q(R16), .clk(Clock));  // open: clr
  Register #(.width(32), .trigger("falling")) register_18 (
    .D(Write_data), .en(and_18_out), .Q(R17), .clk(Clock));  // open: clr
  Register #(.width(32), .trigger("falling")) register_19 (
    .D(Write_data), .en(and_19_out), .Q(R18), .clk(Clock));  // open: clr
  Register #(.width(32), .trigger("falling")) register_20 (
    .D(Write_data), .en(and_20_out), .Q(R19), .clk(Clock));  // open: clr
  Register #(.width(32), .trigger("falling")) register_21 (
    .D(Write_data), .en(and_21_out), .Q(R20), .clk(Clock));  // open: clr
  Register #(.width(32), .trigger("falling")) register_22 (
    .D(Write_data), .en(and_22_out), .Q(R21), .clk(Clock));  // open: clr
  Register #(.width(32), .trigger("falling")) register_23 (
    .D(Write_data), .en(and_23_out), .Q(R22), .clk(Clock));  // open: clr
  Register #(.width(32), .trigger("falling")) register_24 (
    .D(Write_data), .en(and_24_out), .Q(R23), .clk(Clock));  // open: clr
  Register #(.width(32), .trigger("falling")) register_25 (
    .D(Write_data), .en(and_25_out), .Q(R24), .clk(Clock));  // open: clr
  Register #(.width(32), .trigger("falling")) register_26 (
    .D(Write_data), .en(and_26_out), .Q(R25), .clk(Clock));  // open: clr
  Register #(.width(32), .trigger("falling")) register_27 (
    .D(Write_data), .en(and_27_out), .Q(R26), .clk(Clock));  // open: clr
  Register #(.width(32), .trigger("falling")) register_28 (
    .D(Write_data), .en(and_28_out), .Q(R27), .clk(Clock));  // open: clr
  Register #(.width(32), .trigger("falling")) register_29 (
    .D(Write_data), .en(and_29_out), .Q(R28), .clk(Clock));  // open: clr
  Register #(.width(32), .trigger("falling")) register_30 (
    .D(Write_data), .en(and_30_out), .Q(R29), .clk(Clock));  // open: clr
  Register #(.width(32), .trigger("falling")) register_31 (
    .D(Write_data), .en(and_31_out), .Q(R30), .clk(Clock));  // open: clr
  Register #(.width(32), .trigger("falling")) register_32 (
    .D(Write_data), .en(and_32_out), .Q(R31), .clk(Clock));  // open: clr
  Multiplexer #(.select(5), .width(32), .enable("false")) multiplexer_1 (
    .in0(register_1_q), .in1(R1), .in2(R2), .in3(R3), .in4(R4), .in5(R5), .in6(R6), .in7(R7), .in8(R8),
    .in9(R9), .in10(R10), .in11(R11), .in12(R12), .in13(R13), .in14(R14), .in15(R15), .in16(R16), .in17(R17),
    .in18(R18), .in19(R19), .in20(R20), .in21(R21), .in22(R22), .in23(R23), .in24(R24), .in25(R25),
    .in26(R26), .in27(R27), .in28(R28), .in29(R29), .in30(R30), .in31(R31), .out(Read_Data_1),
    .sel(Read_Register_1));
  Multiplexer #(.select(5), .width(32), .enable("false")) multiplexer_2 (
    .in0(register_1_q), .in1(R1), .in2(R2), .in3(R3), .in4(R4), .in5(R5), .in6(R6), .in7(R7), .in8(R8),
    .in9(R9), .in10(R10), .in11(R11), .in12(R12), .in13(R13), .in14(R14), .in15(R15), .in16(R16), .in17(R17),
    .in18(R18), .in19(R19), .in20(R20), .in21(R21), .in22(R22), .in23(R23), .in24(R24), .in25(R25),
    .in26(R26), .in27(R27), .in28(R28), .in29(R29), .in30(R30), .in31(R31), .out(Read_Data_2),
    .sel(Read_Register_2));
endmodule

module ALU_32_bit (
  input  [31:0] A,
  input  [31:0] B,
  input  Carry_In,
  input  Binvert,
  input  Ainvert,
  input  [1:0] Operation,
  input  [2:0] ResCtrl,
  input  [1:0] ShftCtrl,
  input  BranchCtrl,
  input  SLTCtrl,
  output ZeroFlag,
  output [31:0] AluResult,
  output Overflow,
  output Less_sign_flag,
  output less_unsign_flag,
  output Carry_Out
);

  wire alu_1_bit_1_carry_out, alu_1_bit_2_carry_out, alu_1_bit_3_carry_out, alu_1_bit_4_carry_out,
       alu_1_bit_5_carry_out, alu_1_bit_6_carry_out, alu_1_bit_7_carry_out, alu_1_bit_8_carry_out,
       alu_1_bit_9_carry_out, alu_1_bit_10_carry_out, alu_1_bit_11_carry_out, alu_1_bit_12_carry_out,
       alu_1_bit_13_carry_out, alu_1_bit_14_carry_out, alu_1_bit_15_carry_out, alu_1_bit_16_carry_out,
       alu_1_bit_17_carry_out, alu_1_bit_18_carry_out, alu_1_bit_19_carry_out, alu_1_bit_20_carry_out,
       alu_1_bit_21_carry_out, alu_1_bit_22_carry_out, alu_1_bit_23_carry_out, alu_1_bit_24_carry_out,
       alu_1_bit_25_carry_out, alu_1_bit_26_carry_out, alu_1_bit_27_carry_out, alu_1_bit_28_carry_out,
       alu_1_bit_29_carry_out, alu_1_bit_30_carry_out, alu_1_bit_31_carry_out, and_1_out, and_2_out,
       and_3_out, comparator_1_eq, comparator_1_gt, comparator_2_eq, comparator_2_gt, comparator_3_eq,
       comparator_3_gt, comparator_3_lt, multiplexer_1_out, not_1_out, not_3_out, not_4_out, not_5_out,
       not_6_out, not_7_out, not_8_out, or_1_out, R0, R1, R2, R3, R4, R5, R6, R7, R8, R9, R10, R11, R12, R13,
       R14, R15, R16, R17, R18, R19, R20, R21, R22, R23, R24, R25, R26, R27, R28, R29, R30, R31;
  wire [30:0] multiplier_1_out;
  wire [31:0] adder_1_out, adder_2_out, bit_extender_1_out, bit_extender_2_out, bit_extender_3_out,
       bit_extender_4_out, bit_extender_5_out, multiplexer_2_out, multiplexer_3_out, shifter_1_out,
       shifter_2_out, shifter_3_out, shifter_4_out, shifter_5_out;
  wire [31:31] xor_2_out;

  ALU_1_bit alu_1_bit_1 (
    .A(A[0]), .B(B[0]), .Carry_In(Carry_In), .Result(R0), .Carry_Out(alu_1_bit_1_carry_out),
    .Ainvert(Ainvert), .Binvert(Binvert), .Operation(Operation));
  ALU_1_bit alu_1_bit_2 (
    .A(A[1]), .B(B[1]), .Carry_In(alu_1_bit_1_carry_out), .Result(R1), .Carry_Out(alu_1_bit_2_carry_out),
    .Ainvert(Ainvert), .Binvert(Binvert), .Operation(Operation));
  ALU_1_bit alu_1_bit_3 (
    .A(A[2]), .B(B[2]), .Carry_In(alu_1_bit_2_carry_out), .Result(R2), .Carry_Out(alu_1_bit_3_carry_out),
    .Ainvert(Ainvert), .Binvert(Binvert), .Operation(Operation));
  ALU_1_bit alu_1_bit_4 (
    .A(A[3]), .B(B[3]), .Carry_In(alu_1_bit_3_carry_out), .Result(R3), .Carry_Out(alu_1_bit_4_carry_out),
    .Ainvert(Ainvert), .Binvert(Binvert), .Operation(Operation));
  ALU_1_bit alu_1_bit_5 (
    .A(A[4]), .B(B[4]), .Carry_In(alu_1_bit_4_carry_out), .Result(R4), .Carry_Out(alu_1_bit_5_carry_out),
    .Ainvert(Ainvert), .Binvert(Binvert), .Operation(Operation));
  ALU_1_bit alu_1_bit_6 (
    .A(A[5]), .B(B[5]), .Carry_In(alu_1_bit_5_carry_out), .Result(R5), .Carry_Out(alu_1_bit_6_carry_out),
    .Ainvert(Ainvert), .Binvert(Binvert), .Operation(Operation));
  ALU_1_bit alu_1_bit_7 (
    .A(A[6]), .B(B[6]), .Carry_In(alu_1_bit_6_carry_out), .Result(R6), .Carry_Out(alu_1_bit_7_carry_out),
    .Ainvert(Ainvert), .Binvert(Binvert), .Operation(Operation));
  ALU_1_bit alu_1_bit_8 (
    .A(A[7]), .B(B[7]), .Carry_In(alu_1_bit_7_carry_out), .Result(R7), .Carry_Out(alu_1_bit_8_carry_out),
    .Ainvert(Ainvert), .Binvert(Binvert), .Operation(Operation));
  ALU_1_bit alu_1_bit_9 (
    .A(A[8]), .B(B[8]), .Carry_In(alu_1_bit_8_carry_out), .Result(R8), .Carry_Out(alu_1_bit_9_carry_out),
    .Ainvert(Ainvert), .Binvert(Binvert), .Operation(Operation));
  ALU_1_bit alu_1_bit_10 (
    .A(A[9]), .B(B[9]), .Carry_In(alu_1_bit_9_carry_out), .Result(R9), .Carry_Out(alu_1_bit_10_carry_out),
    .Ainvert(Ainvert), .Binvert(Binvert), .Operation(Operation));
  ALU_1_bit alu_1_bit_11 (
    .A(A[10]), .B(B[10]), .Carry_In(alu_1_bit_10_carry_out), .Result(R10),
    .Carry_Out(alu_1_bit_11_carry_out), .Ainvert(Ainvert), .Binvert(Binvert), .Operation(Operation));
  ALU_1_bit alu_1_bit_12 (
    .A(A[11]), .B(B[11]), .Carry_In(alu_1_bit_11_carry_out), .Result(R11),
    .Carry_Out(alu_1_bit_12_carry_out), .Ainvert(Ainvert), .Binvert(Binvert), .Operation(Operation));
  ALU_1_bit alu_1_bit_13 (
    .A(A[12]), .B(B[12]), .Carry_In(alu_1_bit_12_carry_out), .Result(R12),
    .Carry_Out(alu_1_bit_13_carry_out), .Ainvert(Ainvert), .Binvert(Binvert), .Operation(Operation));
  ALU_1_bit alu_1_bit_14 (
    .A(A[13]), .B(B[13]), .Carry_In(alu_1_bit_13_carry_out), .Result(R13),
    .Carry_Out(alu_1_bit_14_carry_out), .Ainvert(Ainvert), .Binvert(Binvert), .Operation(Operation));
  ALU_1_bit alu_1_bit_15 (
    .A(A[14]), .B(B[14]), .Carry_In(alu_1_bit_14_carry_out), .Result(R14),
    .Carry_Out(alu_1_bit_15_carry_out), .Ainvert(Ainvert), .Binvert(Binvert), .Operation(Operation));
  ALU_1_bit alu_1_bit_16 (
    .A(A[15]), .B(B[15]), .Carry_In(alu_1_bit_15_carry_out), .Result(R15),
    .Carry_Out(alu_1_bit_16_carry_out), .Ainvert(Ainvert), .Binvert(Binvert), .Operation(Operation));
  ALU_1_bit alu_1_bit_17 (
    .A(A[16]), .B(B[16]), .Carry_In(alu_1_bit_16_carry_out), .Result(R16),
    .Carry_Out(alu_1_bit_17_carry_out), .Ainvert(Ainvert), .Binvert(Binvert), .Operation(Operation));
  ALU_1_bit alu_1_bit_18 (
    .A(A[17]), .B(B[17]), .Carry_In(alu_1_bit_17_carry_out), .Result(R17),
    .Carry_Out(alu_1_bit_18_carry_out), .Ainvert(Ainvert), .Binvert(Binvert), .Operation(Operation));
  ALU_1_bit alu_1_bit_19 (
    .A(A[18]), .B(B[18]), .Carry_In(alu_1_bit_18_carry_out), .Result(R18),
    .Carry_Out(alu_1_bit_19_carry_out), .Ainvert(Ainvert), .Binvert(Binvert), .Operation(Operation));
  ALU_1_bit alu_1_bit_20 (
    .A(A[19]), .B(B[19]), .Carry_In(alu_1_bit_19_carry_out), .Result(R19),
    .Carry_Out(alu_1_bit_20_carry_out), .Ainvert(Ainvert), .Binvert(Binvert), .Operation(Operation));
  ALU_1_bit alu_1_bit_21 (
    .A(A[20]), .B(B[20]), .Carry_In(alu_1_bit_20_carry_out), .Result(R20),
    .Carry_Out(alu_1_bit_21_carry_out), .Ainvert(Ainvert), .Binvert(Binvert), .Operation(Operation));
  ALU_1_bit alu_1_bit_22 (
    .A(A[21]), .B(B[21]), .Carry_In(alu_1_bit_21_carry_out), .Result(R21),
    .Carry_Out(alu_1_bit_22_carry_out), .Ainvert(Ainvert), .Binvert(Binvert), .Operation(Operation));
  ALU_1_bit alu_1_bit_23 (
    .A(A[22]), .B(B[22]), .Carry_In(alu_1_bit_22_carry_out), .Result(R22),
    .Carry_Out(alu_1_bit_23_carry_out), .Ainvert(Ainvert), .Binvert(Binvert), .Operation(Operation));
  ALU_1_bit alu_1_bit_24 (
    .A(A[23]), .B(B[23]), .Carry_In(alu_1_bit_23_carry_out), .Result(R23),
    .Carry_Out(alu_1_bit_24_carry_out), .Ainvert(Ainvert), .Binvert(Binvert), .Operation(Operation));
  ALU_1_bit alu_1_bit_25 (
    .A(A[24]), .B(B[24]), .Carry_In(alu_1_bit_24_carry_out), .Result(R24),
    .Carry_Out(alu_1_bit_25_carry_out), .Ainvert(Ainvert), .Binvert(Binvert), .Operation(Operation));
  ALU_1_bit alu_1_bit_26 (
    .A(A[25]), .B(B[25]), .Carry_In(alu_1_bit_25_carry_out), .Result(R25),
    .Carry_Out(alu_1_bit_26_carry_out), .Ainvert(Ainvert), .Binvert(Binvert), .Operation(Operation));
  ALU_1_bit alu_1_bit_27 (
    .A(A[26]), .B(B[26]), .Carry_In(alu_1_bit_26_carry_out), .Result(R26),
    .Carry_Out(alu_1_bit_27_carry_out), .Ainvert(Ainvert), .Binvert(Binvert), .Operation(Operation));
  ALU_1_bit alu_1_bit_28 (
    .A(A[27]), .B(B[27]), .Carry_In(alu_1_bit_27_carry_out), .Result(R27),
    .Carry_Out(alu_1_bit_28_carry_out), .Ainvert(Ainvert), .Binvert(Binvert), .Operation(Operation));
  ALU_1_bit alu_1_bit_29 (
    .A(A[28]), .B(B[28]), .Carry_In(alu_1_bit_28_carry_out), .Result(R28),
    .Carry_Out(alu_1_bit_29_carry_out), .Ainvert(Ainvert), .Binvert(Binvert), .Operation(Operation));
  ALU_1_bit alu_1_bit_30 (
    .A(A[29]), .B(B[29]), .Carry_In(alu_1_bit_29_carry_out), .Result(R29),
    .Carry_Out(alu_1_bit_30_carry_out), .Ainvert(Ainvert), .Binvert(Binvert), .Operation(Operation));
  ALU_1_bit alu_1_bit_31 (
    .A(A[30]), .B(B[30]), .Carry_In(alu_1_bit_30_carry_out), .Result(R30),
    .Carry_Out(alu_1_bit_31_carry_out), .Ainvert(Ainvert), .Binvert(Binvert), .Operation(Operation));
  ALU_1_bit alu_1_bit_32 (
    .A(A[31]), .B(B[31]), .Carry_In(alu_1_bit_31_carry_out), .Result(R31), .Carry_Out(Carry_Out),
    .Ainvert(Ainvert), .Binvert(Binvert), .Operation(Operation));
  not not_1 (not_1_out, Carry_Out);
  xor xor_1 (Overflow, alu_1_bit_31_carry_out, Carry_Out);
  or or_1 (or_1_out, R0, R1, R2, R3, R4, R5, R6, R7, R8, R9, R10, R11, R12, R13, R14, R15, R16, R17, R18, R19, R20, R21, R22, R23, R24, R25, R26, R27, R28, R29, R30, R31);
  not not_2 (ZeroFlag, or_1_out);
  Shifter #(.width(32)) shifter_1 (.in(A), .\dist (5'b10000), .out(shifter_1_out));
  assign bit_extender_1_out = {{16{1'b0}}, B[15:0]};  // Bit_Extender bit_extender_1
  Shifter #(.width(32)) shifter_2 (.in(A), .\dist (B[4:0]), .out(shifter_2_out));
  Shifter #(.width(32), .shift("lr")) shifter_3 (.in(A), .\dist (B[4:0]), .out(shifter_3_out));
  Shifter #(.width(32), .shift("ar")) shifter_4 (.in(A), .\dist (B[4:0]), .out(shifter_4_out));
  Shifter #(.width(32), .shift("rr")) shifter_5 (.in(A), .\dist (B[4:0]), .out(shifter_5_out));
  Comparator #(.width(32)) comparator_1 (.a(A), .b(B), .gt(comparator_1_gt), .eq(comparator_1_eq), .lt(Less_sign_flag));
  Comparator #(.width(32), .mode("unsigned")) comparator_2 (
    .a(A), .b(B), .gt(comparator_2_gt), .eq(comparator_2_eq), .lt(less_unsign_flag));
  Comparator #(.width(32), .mode("unsigned")) comparator_3 (
    .a(A), .b(B), .gt(comparator_3_gt), .eq(comparator_3_eq), .lt(comparator_3_lt));
  not not_3 (not_3_out, comparator_1_gt);
  and and_1 (and_1_out, not_3_out, not_4_out, Less_sign_flag);
  not not_4 (not_4_out, comparator_1_eq);
  not not_5 (not_5_out, comparator_2_gt);
  not not_6 (not_6_out, comparator_2_eq);
  and and_2 (and_2_out, not_5_out, not_6_out, less_unsign_flag);
  not not_7 (not_7_out, comparator_3_gt);
  not not_8 (not_8_out, comparator_3_lt);
  Multiplexer #(.enable("false")) multiplexer_1 (.in0(R31), .in1(not_1_out), .out(multiplexer_1_out), .sel(SLTCtrl));
  assign bit_extender_2_out = {{31{1'b0}}, and_1_out};  // Bit_Extender bit_extender_2
  assign bit_extender_3_out = {{31{1'b0}}, and_2_out};  // Bit_Extender bit_extender_3
  assign bit_extender_4_out = {{31{1'b0}}, and_3_out};  // Bit_Extender bit_extender_4
  and and_3 (and_3_out, not_7_out, comparator_3_eq, not_8_out);
  Multiplier #(.width(31)) multiplier_1 (.a(A[30:0]), .b(B[30:0]), .out(multiplier_1_out));  // open: cin, cout
  xor xor_2 (xor_2_out[31], A[31], B[31]);
  Adder #(.width(32)) adder_1 (.a(B), .b({32{1'b0}}), .out(adder_1_out), .cin(1'b0));  // open: cout
  Adder #(.width(32)) adder_2 (.a(shifter_1_out), .b(bit_extender_1_out), .out(adder_2_out), .cin(1'b0));  // open: cout
  Multiplexer #(.select(2), .width(32), .enable("false")) multiplexer_2 (
    .in0(shifter_2_out), .in1(shifter_3_out), .in2(shifter_4_out), .in3(shifter_5_out),
    .out(multiplexer_2_out), .sel(ShftCtrl));
  Multiplexer #(.width(32), .enable("false")) multiplexer_3 (
    .in0(bit_extender_2_out), .in1(bit_extender_3_out), .out(multiplexer_3_out), .sel(BranchCtrl));
  assign bit_extender_5_out = {{31{1'b0}}, multiplexer_1_out};  // Bit_Extender bit_extender_5
  Multiplexer #(.select(3), .width(32), .enable("false")) multiplexer_4 (
    .in0({R31, R30, R29, R28, R27, R26, R25, R24, R23, R22, R21, R20, R19, R18, R17, R16, R15, R14, R13, R12, R11, R10, R9, R8, R7, R6, R5, R4, R3, R2, R1, R0}),
    .in1(multiplexer_2_out), .in2(multiplexer_3_out), .in3(bit_extender_4_out), .in4(bit_extender_5_out),
    .in5({xor_2_out[31], multiplier_1_out}), .in6(adder_1_out), .in7(adder_2_out), .out(AluResult),
    .sel(ResCtrl));

  // Other names for the same wires on the sheet: b_t[4:0] = B[4:0]

  // Notes on the sheet:
  //   SLL
  //   SRL
  //   SRA
  //   ROR
  //   BEQ / BNE
  //   BEQ / BNE
  //   SEQ
  //   SLT
  //   MUL
  //   SET
  //   SSET
  //   Signed
  //   Unsigned
endmodule

module Next_PC (
  input  [4:0] ImmL_5,
  input  [10:0] ImmU_11,
  input  [15:0] Imm_16,
  input  jump,
  input  branch,
  input  [31:0] Rs1,
  input  Clock,
  output [19:0] Instruction_Address,
  output [19:0] PC_1
);

  wire [19:0] adder_2_out, adder_3_out, bit_extender_1_out, multiplexer_1_out, multiplexer_2_out;
  wire [31:0] bit_extender_2_out, Rs1_q;
  wire [31:20] adder_3_out_2;

  Register #(.width(20), .trigger("falling")) PC (
    .D(multiplexer_2_out), .en(1'b1), .Q(Instruction_Address), .clk(Clock));  // open: clr
  Adder #(.width(20)) adder_1 (.a(Instruction_Address), .b(20'h1), .out(PC_1));  // open: cin, cout
  // Probe on PC_1
  assign bit_extender_1_out = {{4{ImmU_11[10]}}, {ImmU_11, ImmL_5}};  // Bit_Extender bit_extender_1
  assign bit_extender_2_out = {{16{Imm_16[15]}}, Imm_16};  // Bit_Extender bit_extender_2
  Register #(.width(32), .trigger("high")) u_Rs1 (.D(Rs1), .en(1'b1), .Q(Rs1_q), .clk(Clock));  // open: clr
  Adder #(.width(20)) adder_2 (
    .a(Instruction_Address), .b(bit_extender_1_out), .out(adder_2_out), .cin(1'b0));  // open: cout
  Adder #(.width(32)) adder_3 (
    .a(bit_extender_2_out), .b(Rs1_q), .out({adder_3_out_2, adder_3_out}), .cin(1'b0));  // open: cout
  // Probe on adder_2_out
  // Probe on adder_3_out
  Multiplexer #(.width(20), .enable("false")) multiplexer_1 (
    .in0(PC_1), .in1(adder_2_out), .out(multiplexer_1_out), .sel(branch));
  Multiplexer #(.width(20), .enable("false")) multiplexer_2 (
    .in0(multiplexer_1_out), .in1(adder_3_out), .out(multiplexer_2_out), .sel(jump));

  // Notes on the sheet:
  //   PC + 1
  //   PC + 1
endmodule

module ALU_1_bit (
  input  A,
  input  Ainvert,
  input  B,
  input  Binvert,
  input  [1:0] Operation,
  input  Carry_In,
  output Result,
  output Carry_Out
);

  wire adder_1_out, and_1_out, multiplexer_1_out, multiplexer_2_out, not_1_out, not_2_out, or_1_out,
       xor_1_out;

  Multiplexer #(.enable("false")) multiplexer_1 (.in0(A), .in1(not_1_out), .out(multiplexer_1_out), .sel(Ainvert));
  not not_1 (not_1_out, A);
  Multiplexer #(.enable("false")) multiplexer_2 (.in0(B), .in1(not_2_out), .out(multiplexer_2_out), .sel(Binvert));
  not not_2 (not_2_out, B);
  and and_1 (and_1_out, multiplexer_1_out, multiplexer_2_out);
  or or_1 (or_1_out, multiplexer_1_out, multiplexer_2_out);
  xor xor_1 (xor_1_out, multiplexer_1_out, multiplexer_2_out);
  Adder #(.width(1)) adder_1 (
    .a(multiplexer_1_out), .b(multiplexer_2_out), .out(adder_1_out), .cin(Carry_In), .cout(Carry_Out));
  Multiplexer #(.select(2), .enable("false")) multiplexer_3 (
    .in0(and_1_out), .in1(or_1_out), .in2(xor_1_out), .in3(adder_1_out), .out(Result), .sel(Operation));
endmodule

module Main_Control_Unit (
  input  [5:0] Opcode,
  output SW,
  output R_TypeEnable,
  output RegWrite,
  output ALUsrc,
  output MemRead,
  output MemWrite,
  output MemToReg,
  output Branch,
  output Jump,
  output ExtOp,
  output sset
);

  wire and_1_out, and_2_out, and_4_out, and_5_out, and_6_out, and_7_out, and_8_out, and_9_out, and_10_out,
       and_11_out, and_14_out, and_15_out, and_16_out, and_17_out, and_18_out, and_19_out, not_1_out,
       not_2_out, not_3_out, not_4_out, not_5_out, not_6_out, not_7_out, not_8_out, not_9_out, not_10_out,
       not_11_out, not_12_out, not_13_out, not_14_out, not_15_out, not_16_out, not_17_out, not_18_out,
       not_19_out, not_20_out, not_21_out, not_22_out, not_23_out, not_24_out, not_25_out, not_26_out,
       not_27_out, not_28_out, not_29_out, not_30_out, not_31_out, or_2_out;

  not not_1 (not_1_out, Opcode[2]);
  not not_2 (not_2_out, Opcode[1]);
  not not_3 (not_3_out, Opcode[0]);
  not not_4 (not_4_out, Opcode[4]);
  not not_5 (not_5_out, Opcode[3]);
  not not_6 (not_6_out, Opcode[4]);
  not not_7 (not_7_out, Opcode[3]);
  not not_8 (not_8_out, Opcode[4]);
  not not_9 (not_9_out, Opcode[3]);
  not not_10 (not_10_out, Opcode[2]);
  not not_11 (not_11_out, Opcode[1]);
  not not_12 (not_12_out, Opcode[0]);
  not not_13 (not_13_out, Opcode[2]);
  not not_14 (not_14_out, Opcode[1]);
  not not_15 (not_15_out, Opcode[2]);
  not not_16 (not_16_out, Opcode[1]);
  not not_17 (not_17_out, Opcode[0]);
  not not_18 (not_18_out, Opcode[2]);
  not not_19 (not_19_out, Opcode[1]);
  not not_20 (not_20_out, Opcode[0]);
  and and_1 (and_1_out, Opcode[4], Opcode[1]);
  and and_2 (and_2_out, Opcode[4], Opcode[2]);
  and and_3 (Jump, Opcode[3], Opcode[2], Opcode[1], Opcode[0]);
  not not_21 (not_21_out, Opcode[2]);
  not not_22 (not_22_out, Opcode[1]);
  not not_23 (not_23_out, Opcode[0]);
  not not_24 (not_24_out, Opcode[1]);
  not not_25 (not_25_out, Opcode[0]);
  not not_26 (not_26_out, Opcode[3]);
  not not_27 (not_27_out, Opcode[2]);
  not not_28 (not_28_out, Opcode[1]);
  not not_29 (not_29_out, Opcode[4]);
  and and_4 (and_4_out, not_1_out, not_2_out, not_3_out);
  and and_5 (and_5_out, not_4_out, not_5_out, Opcode[0]);
  and and_6 (and_6_out, not_6_out, not_7_out, Opcode[1]);
  and and_7 (and_7_out, not_8_out, not_9_out, Opcode[2]);
  and and_8 (and_8_out, Opcode[3], not_10_out);
  and and_9 (and_9_out, Opcode[3], not_11_out);
  and and_10 (and_10_out, Opcode[3], not_12_out);
  and and_11 (and_11_out, Opcode[4], not_13_out, not_14_out);
  and and_12 (MemRead, Opcode[4], not_15_out, not_16_out, not_17_out);
  and and_13 (MemWrite, Opcode[4], not_18_out, not_19_out, Opcode[0]);
  and and_14 (and_14_out, Opcode[4], not_20_out);
  and and_15 (and_15_out, Opcode[4], Opcode[1]);
  or or_1 (Branch, and_1_out, and_2_out);
  and and_16 (and_16_out, not_21_out, not_22_out, not_23_out);
  and and_17 (and_17_out, Opcode[2], not_24_out, Opcode[0]);
  and and_18 (and_18_out, Opcode[2], Opcode[1], not_25_out);
  and and_19 (and_19_out, Opcode[3], Opcode[2], Opcode[1]);
  not not_30 (not_30_out, Opcode[0]);
  and and_20 (sset, not_30_out, Opcode[1], Opcode[2], Opcode[3], not_31_out);
  not not_31 (not_31_out, Opcode[4]);
  and and_21 (SW, Opcode[4], not_26_out, not_27_out, not_28_out, Opcode[0]);
  not not_32 (R_TypeEnable, or_2_out);
  or or_2 (or_2_out, Opcode[4], Opcode[3], Opcode[2], Opcode[1], Opcode[0]);
  or or_3 (RegWrite, not_29_out, and_4_out);
  or or_4 (ALUsrc, and_5_out, and_6_out, and_7_out, and_8_out, and_9_out, and_10_out, and_11_out);
  or or_5 (MemToReg, and_14_out, and_15_out);
  or or_6 (ExtOp, and_16_out, and_17_out, and_18_out, and_19_out, Opcode[4]);
endmodule

module Full_Processor (
);

  wire alu_32_bit_1_p10, alu_32_bit_1_p15, alu_32_bit_1_p16, alucontrol_unit_1_p2, alucontrol_unit_1_p4,
       alucontrol_unit_1_p6, alucontrol_unit_1_p8, alucontrol_unit_1_p12, alucontrol_unit_1_p14, and_1_out,
       Branch, branch_control_unit_1_p2, branch_control_unit_1_p3, branch_control_unit_1_p4,
       branch_control_unit_1_p5, clock_1_out, jump, main_control_unit_1_p1, main_control_unit_1_p2,
       main_control_unit_1_p5, main_control_unit_1_p8, main_control_unit_1_p10, main_control_unit_1_p11, R,
       sset, w;
  wire [4:0] IMM16, IMML, multiplexer_2_out, Rs1;
  wire [5:0] OP;
  wire [10:0] func;
  wire [19:0] next_pc_1_instruction_address, next_pc_1_pc_1;
  wire [31:0] alu_32_bit_1_p14, bit_extender_1_out, bit_extender_2_out, bit_extender_3_out,
       bit_extender_4_out, data_memory_1_p6, multiplexer_1_out, multiplexer_3_out, multiplexer_4_out,
       multiplexer_5_out, multiplexer_6_out, R1, R2, R3, R4, R5, R6, R7, R8, R9, R10, R11, R12, R13, R14,
       R15, R16, R17, R18, R19, R20, R21, R22, R23, R24, R25, R26, R27, R28, R29, R30, R31,
       register_file_1_read_data_1, register_file_1_read_data_2;

  ROM #(.addrWidth(20), .dataWidth(32)) rom_1 (
    .addr(next_pc_1_instruction_address), .data({func, IMM16, Rs1, IMML, OP}));  // open: sel
  // Main_Control_Unit main_control_unit_1: pin names not known; wires that end beside it: main_control_unit_1_p1, main_control_unit_1_p2, R, w, main_control_unit_1_p5, Branch, jump, main_control_unit_1_p8, sset, main_control_unit_1_p10, main_control_unit_1_p11
  // Probe on next_pc_1_instruction_address
  Clock clock_1 (.out(clock_1_out));
  Next_PC next_pc_1 (
    .ImmL_5(IMML), .ImmU_11(func), .Imm_16({func, IMM16}), .Rs1(register_file_1_read_data_1),
    .branch(and_1_out), .jump(jump), .PC_1(next_pc_1_pc_1),
    .Instruction_Address(next_pc_1_instruction_address), .Clock(clock_1_out));
  // Probe on R1
  assign bit_extender_1_out = {{12{1'b0}}, next_pc_1_pc_1};  // Bit_Extender bit_extender_1
  assign bit_extender_2_out = {{16{1'b0}}, {func, IMM16}};  // Bit_Extender bit_extender_2
  assign bit_extender_3_out = {{16{func[10]}}, {func, IMM16}};  // Bit_Extender bit_extender_3
  // Probe on R2
  // Probe on R3
  Multiplexer #(.width(32), .enable("false")) multiplexer_1 (
    .in0(bit_extender_2_out), .in1(bit_extender_3_out), .out(multiplexer_1_out), .sel(main_control_unit_1_p8));
  // Probe on R4
  assign bit_extender_4_out = {{16{func[10]}}, {func, IMML}};  // Bit_Extender bit_extender_4
  // Probe on R6
  // Probe on R5
  Multiplexer #(.width(5), .enable("false")) multiplexer_2 (.in0(Rs1), .in1(IMML), .out(multiplexer_2_out), .sel(sset));
  // Probe on R7
  // Probe on R8
  // Probe on R9
  // Probe on R10
  // Probe on R11
  // Probe on R12
  Register_File register_file_1 (
    .Write_data(multiplexer_6_out), .Read_Register_2(IMM16), .Read_Data_1(register_file_1_read_data_1),
    .Read_Data_2(register_file_1_read_data_2), .Read_Register_1(multiplexer_2_out), .Write_Register(IMML),
    .RegWrite(main_control_unit_1_p1), .Clock(clock_1_out), .R1(R1), .R2(R2), .R4(R4), .R3(R3), .R6(R6),
    .R5(R5), .R8(R8), .R7(R7), .R15(R15), .R14(R14), .R13(R13), .R12(R12), .R11(R11), .R10(R10), .R9(R9),
    .R16(R16), .R17(R17), .R18(R18), .R19(R19), .R20(R20), .R21(R21), .R22(R22), .R23(R23), .R24(R24),
    .R25(R25), .R26(R26), .R27(R27), .R28(R28), .R29(R29), .R30(R30), .R31(R31));
  // Probe on R14
  // Probe on R13
  // Probe on R15
  // Probe on R16
  // Probe on R17
  Multiplexer #(.width(32), .enable("false")) multiplexer_3 (
    .in0(register_file_1_read_data_2), .in1(multiplexer_1_out), .out(multiplexer_3_out),
    .sel(main_control_unit_1_p2));
  // Probe on R18
  // Probe on R19
  // Probe on R20
  // Probe on R22
  // Probe on R21
  Multiplexer #(.width(32), .enable("false")) multiplexer_4 (
    .in0(multiplexer_3_out), .in1(bit_extender_4_out), .out(multiplexer_4_out), .sel(main_control_unit_1_p11));
  // Probe on R23
  // ALUControl_Unit alucontrol_unit_1: pin names not known; wires that end beside it: clock_1_out, alucontrol_unit_1_p2, clock_1_out, alucontrol_unit_1_p4, clock_1_out, alucontrol_unit_1_p6, clock_1_out, alucontrol_unit_1_p8, clock_1_out, clock_1_out, clock_1_out, alucontrol_unit_1_p12, clock_1_out, alucontrol_unit_1_p14
  // Probe on R24
  // Probe on R25
  // Branch_control_unit branch_control_unit_1: pin names not known; wires that end beside it: OP, branch_control_unit_1_p2, branch_control_unit_1_p3, branch_control_unit_1_p4, branch_control_unit_1_p5
  // Probe on R26
  // Probe on R27
  // Probe on R28
  and and_1 (and_1_out, Branch, branch_control_unit_1_p5);
  // ALU_32_bit alu_32_bit_1: pin names not known; wires that end beside it: register_file_1_read_data_1, multiplexer_4_out, alucontrol_unit_1_p2, alucontrol_unit_1_p4, alucontrol_unit_1_p6, alucontrol_unit_1_p8, clock_1_out, alucontrol_unit_1_p14, alucontrol_unit_1_p12, alu_32_bit_1_p10, branch_control_unit_1_p2, branch_control_unit_1_p4, branch_control_unit_1_p3, alu_32_bit_1_p14, alu_32_bit_1_p15, alu_32_bit_1_p16
  // Probe on R30
  // Probe on R29
  // Probe on alu_32_bit_1_p15
  // Probe on alu_32_bit_1_p16
  // Probe on R31
  // Data_Memory data_memory_1: pin names not known; wires that end beside it: alu_32_bit_1_p14, register_file_1_read_data_2, w, clock_1_out, R, data_memory_1_p6
  Multiplexer #(.width(32), .enable("false")) multiplexer_5 (
    .in0(alu_32_bit_1_p14), .in1(data_memory_1_p6), .out(multiplexer_5_out), .sel(main_control_unit_1_p5));
  Multiplexer #(.width(32), .enable("false")) multiplexer_6 (
    .in0(multiplexer_5_out), .in1(bit_extender_1_out), .out(multiplexer_6_out), .sel(jump));

  // Other names for the same wires on the sheet: Rs2[4:0] = IMM16; Rd[4:0] = IMML; IMM16[15:5] = func;
  //   IMMU[10:0] = func

  // Notes on the sheet:
  //   contents of rom_1 (hex, n*v repeats v):
  //   1004d 10011 10051 a008d 20091 128900cd 45ac00ce 230711 500010d 7342010e 240751 384004d 1234020d
  //   5678020e 140945 12508c0 834100 50 10090 200d0 a42100 841100 c31180 30d2 820880 ffe00712 40011
  //   1a31280 245380 4453c0 57684 2501cf 4545024d 4545028d 95095 ffff0dcb 12 1431140 50 50890 608d0
  //   1631100 40011 380f
endmodule

module Instruction_Memory (
  output [5:0] out_1,
  output [4:0] out_2,
  output [4:0] out_3,
  output [4:0] out_4,
  output [10:0] out_5,
  output [15:0] out_6
);

  wire [19:0] undriven;

  ROM #(.addrWidth(20), .dataWidth(32)) rom_1 (
    .addr(undriven), .data({out_5, out_4, out_3, out_2, out_1}));  // open: sel

  assign out_6 = {out_5, out_4};

  // Other names for the same wires on the sheet: OP[5:0] = out_1; IMML[4:0] = out_2; Rd[4:0] = out_2; Rs[4:0] = out_3;
  //   IMM16[15:0] = {out_5, out_4}; Rt[4:0] = out_4; IMMU[10:0] = out_5

  // Notes on the sheet:
  //   contents of rom_1 (hex, n*v repeats v):
  //   1004d 10011 10051 a008d 20091 128900cd 45ac00ce 230711 500010d 7342010e 240751 384004d 1234020d
  //   5678020e 140945 12508c0 834100 50 10090 200d0 a42100 841100 c31180 30d2 820880 ffe00712 40011
  //   1a31280 245380 4453c0 57684 2501cf 4545024d 4545028d 95095 ffff0dcb 12 1431140 50 50890 608d0
  //   1631100 40011 380f
endmodule

module Data_Memory (
  input  in_1,
  input  in_2,
  input  in_3,
  input  [31:0] in_4,
  input  [19:0] in_5,
  output [31:0] out_6
);

  wire [19:0] undriven;

  RAM #(.addrWidth(20), .dataWidth(32), .bus("separate")) ram_1 (
    .addr(undriven), .din(in_4), .data(out_6), .str(in_2), .clk(in_1), .ld(in_3));  // open: sel, clr

  // Other names for the same wires on the sheet: AluResuit[19:0] = in_5; BusB[31:0] = in_4; Memory_Read = in_3;
  //   Memory_Write = in_2
endmodule

module Branch_control_unit (
  input  [5:0] in_1,
  input  zero_flag,
  input  less_sign_flag,
  input  Branch,
  input  less_unsign_flag,
  output BranchTaken
);

  wire and_1_out, and_2_out, and_3_out, and_4_out, and_5_out, and_6_out, not_1_out, not_2_out, not_3_out,
       not_4_out, not_5_out, not_6_out, not_7_out, not_8_out, not_9_out, not_10_out, not_11_out, not_12_out,
       not_13_out, not_14_out, not_15_out, not_16_out, or_1_out;

  not not_1 (not_1_out, in_1[0]);
  not not_2 (not_2_out, in_1[2]);
  not not_3 (not_3_out, in_1[3]);
  not not_4 (not_4_out, in_1[2]);
  not not_5 (not_5_out, in_1[3]);
  not not_6 (not_6_out, zero_flag);
  not not_7 (not_7_out, in_1[0]);
  not not_8 (not_8_out, in_1[1]);
  not not_9 (not_9_out, in_1[3]);
  not not_10 (not_10_out, in_1[1]);
  not not_11 (not_11_out, in_1[3]);
  not not_12 (not_12_out, less_sign_flag);
  not not_13 (not_13_out, in_1[0]);
  not not_14 (not_14_out, in_1[3]);
  not not_15 (not_15_out, in_1[3]);
  not not_16 (not_16_out, less_unsign_flag);
  and and_1 (and_1_out, not_1_out, in_1[1], not_2_out, not_3_out, in_1[4], zero_flag);
  and and_2 (and_2_out, in_1[0], in_1[1], not_4_out, not_5_out, in_1[4], not_6_out);
  and and_3 (and_3_out, not_7_out, not_8_out, in_1[2], not_9_out, in_1[4], less_sign_flag);
  and and_4 (and_4_out, in_1[0], not_10_out, in_1[2], not_11_out, in_1[4], not_12_out);
  and and_5 (and_5_out, not_13_out, in_1[1], in_1[2], not_14_out, in_1[4], less_unsign_flag);
  and and_6 (and_6_out, in_1[0], in_1[1], in_1[2], not_15_out, in_1[4], not_16_out);
  or or_1 (or_1_out, and_1_out, and_2_out, and_3_out, and_4_out, and_5_out, and_6_out);
  and and_7 (BranchTaken, or_1_out, Branch);

  // Notes on the sheet:
  //   opcode
  //   BEQ
  //   BNE
  //   BLT
  //   BGT
  //   BLTU
  //   BGTU
endmodule

module ALUControl_Unit (
  input  [10:0] Func,
  input  [5:0] OpCode,
  input  Rtype_Enable,
  output CarryIn,
  output Ainvert,
  output Binvert,
  output [1:0] Operation,
  output SLTCtrl,
  output BranchCtrl,
  output [1:0] ShftCtrl,
  output [2:0] ResCtrl
);

  wire and_2_out, and_3_out, and_4_out, and_5_out, and_6_out, and_8_out, and_9_out, and_10_out, and_11_out,
       and_12_out, and_13_out, and_14_out, and_15_out, and_16_out, and_17_out, and_18_out, and_19_out,
       and_20_out, and_21_out, and_22_out, and_23_out, and_24_out, and_25_out, and_26_out, and_27_out,
       and_28_out, and_29_out, not_1_out, not_2_out, not_3_out, not_4_out, not_5_out, not_6_out, not_7_out,
       not_8_out, not_9_out, not_10_out, not_11_out, not_12_out, not_13_out, not_14_out, not_15_out,
       not_16_out, not_17_out, not_18_out, not_19_out, not_20_out, not_21_out, not_22_out, not_23_out,
       not_24_out, not_25_out, not_26_out, not_27_out, not_28_out, not_29_out, not_30_out, not_31_out,
       not_32_out, not_33_out, not_34_out, not_35_out, not_36_out, not_37_out;
  wire [11:0] bit_extender_1_out;
  wire [11:1] multiplexer_1_out;

  assign bit_extender_1_out = {{6{1'b0}}, OpCode};  // Bit_Extender bit_extender_1
  Multiplexer #(.width(12), .enable("false")) multiplexer_1 (
    .in0(bit_extender_1_out), .in1({1'b1, Func}), .out({multiplexer_1_out, SLTCtrl}), .sel(Rtype_Enable));
  not not_1 (not_1_out, multiplexer_1_out[3]);
  not not_2 (not_2_out, multiplexer_1_out[1]);
  not not_3 (not_3_out, SLTCtrl);
  not not_4 (not_4_out, multiplexer_1_out[3]);
  not not_5 (not_5_out, multiplexer_1_out[1]);
  not not_6 (not_6_out, SLTCtrl);
  not not_7 (not_7_out, multiplexer_1_out[3]);
  not not_8 (not_8_out, multiplexer_1_out[2]);
  not not_9 (not_9_out, multiplexer_1_out[1]);
  not not_10 (not_10_out, multiplexer_1_out[2]);
  not not_11 (not_11_out, SLTCtrl);
  and and_1 (BranchCtrl, multiplexer_1_out[2], multiplexer_1_out[1]);
  and and_2 (and_2_out, multiplexer_1_out[1], SLTCtrl);
  and and_3 (and_3_out, multiplexer_1_out[11], multiplexer_1_out[1]);
  not not_12 (not_12_out, multiplexer_1_out[11]);
  not not_13 (not_13_out, SLTCtrl);
  not not_14 (not_14_out, multiplexer_1_out[3]);
  not not_15 (not_15_out, SLTCtrl);
  not not_16 (not_16_out, multiplexer_1_out[1]);
  not not_17 (not_17_out, multiplexer_1_out[2]);
  not not_18 (not_18_out, multiplexer_1_out[1]);
  not not_19 (not_19_out, SLTCtrl);
  not not_20 (not_20_out, multiplexer_1_out[11]);
  not not_21 (not_21_out, multiplexer_1_out[1]);
  not not_22 (not_22_out, SLTCtrl);
  not not_23 (not_23_out, multiplexer_1_out[11]);
  not not_24 (not_24_out, multiplexer_1_out[4]);
  not not_25 (not_25_out, multiplexer_1_out[3]);
  not not_26 (not_26_out, multiplexer_1_out[1]);
  not not_27 (not_27_out, SLTCtrl);
  not not_28 (not_28_out, multiplexer_1_out[4]);
  not not_29 (not_29_out, multiplexer_1_out[3]);
  not not_30 (not_30_out, multiplexer_1_out[2]);
  not not_31 (not_31_out, multiplexer_1_out[4]);
  not not_32 (not_32_out, multiplexer_1_out[2]);
  not not_33 (not_33_out, multiplexer_1_out[1]);
  not not_34 (not_34_out, SLTCtrl);
  not not_35 (not_35_out, SLTCtrl);
  and and_4 (and_4_out, not_1_out, multiplexer_1_out[1]);
  and and_5 (and_5_out, multiplexer_1_out[4], multiplexer_1_out[2]);
  and and_6 (and_6_out, multiplexer_1_out[11], SLTCtrl);
  and and_7 (Ainvert, multiplexer_1_out[3], multiplexer_1_out[2], not_2_out, not_3_out);
  and and_8 (and_8_out, not_4_out, multiplexer_1_out[2], multiplexer_1_out[1]);
  and and_9 (and_9_out, multiplexer_1_out[3], multiplexer_1_out[2], not_5_out, not_6_out);
  and and_10 (and_10_out, multiplexer_1_out[4], multiplexer_1_out[1]);
  and and_11 (and_11_out, multiplexer_1_out[4], multiplexer_1_out[2]);
  and and_12 (and_12_out, multiplexer_1_out[11], not_7_out, multiplexer_1_out[2], SLTCtrl);
  not not_36 (not_36_out, multiplexer_1_out[3]);
  and and_13 (and_13_out, not_8_out, not_9_out);
  and and_14 (and_14_out, multiplexer_1_out[2], multiplexer_1_out[1]);
  not not_37 (not_37_out, multiplexer_1_out[3]);
  and and_15 (and_15_out, not_10_out, not_11_out);
  and and_16 (and_16_out, multiplexer_1_out[2], multiplexer_1_out[1]);
  or or_1 (ShftCtrl[1], and_2_out, multiplexer_1_out[2], and_3_out);
  and and_17 (and_17_out, not_12_out, not_13_out);
  and and_18 (and_18_out, multiplexer_1_out[11], SLTCtrl);
  and and_19 (and_19_out, not_14_out, multiplexer_1_out[2], multiplexer_1_out[1]);
  and and_20 (and_20_out, multiplexer_1_out[2], multiplexer_1_out[1], not_15_out);
  and and_21 (and_21_out, multiplexer_1_out[3], multiplexer_1_out[2], not_16_out, SLTCtrl);
  and and_22 (and_22_out, multiplexer_1_out[3], not_17_out, not_18_out, not_19_out);
  and and_23 (and_23_out, not_20_out, multiplexer_1_out[3], multiplexer_1_out[2], not_21_out, SLTCtrl);
  and and_24 (and_24_out, multiplexer_1_out[3], multiplexer_1_out[2], multiplexer_1_out[1], not_22_out);
  and and_25 (and_25_out, not_23_out, not_24_out, not_25_out, not_26_out, not_27_out);
  and and_26 (and_26_out, not_28_out, not_29_out, not_30_out);
  and and_27 (and_27_out, not_31_out, not_32_out, not_33_out, not_34_out);
  and and_28 (and_28_out, multiplexer_1_out[3], multiplexer_1_out[2], multiplexer_1_out[1], not_35_out);
  and and_29 (and_29_out, multiplexer_1_out[11], multiplexer_1_out[3], multiplexer_1_out[2], SLTCtrl);
  or or_2 (CarryIn, and_4_out, and_5_out, and_6_out);
  or or_3 (Binvert, and_8_out, and_9_out, and_10_out, and_11_out, and_12_out);
  or or_4 (Operation[1], not_36_out, and_13_out, and_14_out);
  or or_5 (Operation[0], not_37_out, and_15_out, and_16_out);
  or or_6 (ShftCtrl[0], and_17_out, and_18_out);
  or or_7 (ResCtrl[2], and_19_out, and_20_out, and_21_out);
  or or_8 (ResCtrl[1], and_22_out, and_23_out, and_24_out);
  or or_9 (ResCtrl[0], and_25_out, and_26_out, and_27_out, and_28_out, and_29_out);
endmodule

module IF_ID (
  input  [19:0] PC__1,
  input  [31:0] Instruction,
  input  En,
  input  Clock,
  output [19:0] PC_1,
  output [31:0] Instruction_2
);

  wire not_1_out;

  not not_1 (not_1_out, En);
  Register #(.width(20)) register_1 (.D(PC__1), .en(not_1_out), .Q(PC_1), .clk(Clock));  // open: clr
  Register #(.width(32)) register_2 (.D(Instruction), .en(not_1_out), .Q(Instruction_2), .clk(Clock));  // open: clr
endmodule

module ID_EX (
  input  [19:0] PC_1,
  input  [4:0] Rd,
  input  [31:0] IMM,
  input  [31:0] A,
  input  [31:0] B,
  input  [18:0] Control_Signals,
  input  Clock,
  output [19:0] PC_1_2,
  output [4:0] Rd_2,
  output [31:0] IMM_2,
  output [31:0] A_2,
  output [31:0] B_2,
  output [18:0] Control_Signals_2
);

  Register #(.width(20)) register_1 (.D(PC_1), .en(1'b1), .Q(PC_1_2), .clk(Clock));  // open: clr
  Register #(.width(5)) register_2 (.D(Rd), .en(1'b1), .Q(Rd_2), .clk(Clock));  // open: clr
  Register #(.width(32)) register_3 (.D(IMM), .en(1'b1), .Q(IMM_2), .clk(Clock));  // open: clr
  Register #(.width(32)) register_4 (.D(A), .en(1'b1), .Q(A_2), .clk(Clock));  // open: clr
  Register #(.width(32)) register_5 (.D(B), .en(1'b1), .Q(B_2), .clk(Clock));  // open: clr
  Register #(.width(19)) register_6 (.D(Control_Signals), .en(1'b1), .Q(Control_Signals_2), .clk(Clock));  // open: clr
endmodule

module EX_MEM (
  input  [19:0] ALUres,
  input  [4:0] Rd,
  input  [31:0] B,
  input  [3:0] Control_Signals,
  input  Clock,
  output [19:0] ALUres_2,
  output [4:0] Rd_2,
  output [31:0] B_2,
  output [3:0] Control_Signals_2
);

  Register #(.width(20)) register_1 (.D(ALUres), .en(1'b1), .Q(ALUres_2), .clk(Clock));  // open: clr
  Register #(.width(5)) register_2 (.D(Rd), .en(1'b1), .Q(Rd_2), .clk(Clock));  // open: clr
  Register #(.width(32)) register_3 (.D(B), .en(1'b1), .Q(B_2), .clk(Clock));  // open: clr
  Register #(.width(4)) register_4 (.D(Control_Signals), .en(1'b1), .Q(Control_Signals_2), .clk(Clock));  // open: clr
endmodule

module MEM_WB (
  input  [31:0] DataOut,
  input  [4:0] in_2,
  input  RegWr,
  input  Clock,
  output [31:0] DataOut_2,
  output [4:0] Rd,
  output RegWr_2
);

  Register #(.width(32)) register_1 (.D(DataOut), .en(1'b1), .Q(DataOut_2), .clk(Clock));  // open: clr
  Register #(.width(5)) register_2 (.D(in_2), .en(1'b1), .Q(Rd), .clk(Clock));  // open: clr
  Register #(.width(1)) register_3 (.D(RegWr), .en(1'b1), .Q(RegWr_2), .clk(Clock));  // open: clr
endmodule

module Extender (
  input  [19:0] PC,
  input  [4:0] IMML,
  input  [10:0] IMMU,
  input  [15:0] IMM16,
  input  [31:0] Rs1,
  input  Clock,
  input  ExtOp,
  output [19:0] Branch_Address,
  output [31:0] BusB___immULExtended,
  output [19:0] Jump_Address,
  output [31:0] IMM16_2
);

  wire [19:0] bit_extender_4_out;
  wire [31:0] bit_extender_1_out, bit_extender_2_out, bit_extender_3_out, Rs1_q;
  wire [31:20] adder_1_out;

  assign bit_extender_1_out = {{16{IMM16[15]}}, IMM16};  // Bit_Extender bit_extender_1
  Register #(.width(32), .trigger("high")) u_Rs1 (.D(Rs1), .en(1'b1), .Q(Rs1_q), .clk(Clock));  // open: clr
  assign bit_extender_2_out = {{16{1'b0}}, IMM16};  // Bit_Extender bit_extender_2
  assign bit_extender_3_out = {{16{IMM16[15]}}, IMM16};  // Bit_Extender bit_extender_3
  Multiplexer #(.width(32), .enable("false")) multiplexer_1 (
    .in0(bit_extender_2_out), .in1(bit_extender_3_out), .out(IMM16_2), .sel(ExtOp));
  assign bit_extender_4_out = {{4{IMMU[10]}}, {IMMU, IMML}};  // Bit_Extender bit_extender_4
  assign BusB___immULExtended = {{16{IMMU[10]}}, {IMMU, IMML}};  // Bit_Extender bit_extender_5
  Adder #(.width(32)) adder_1 (
    .a(bit_extender_1_out), .b(Rs1_q), .out({adder_1_out, Jump_Address}), .cin(1'b0));  // open: cout
  Adder #(.width(20)) adder_2 (.a(PC), .b(bit_extender_4_out), .out(Branch_Address), .cin(1'b0));  // open: cout

  // Notes on the sheet:
  //   immU,immL Extended
  //   imm16 extended
  //   20-bit branch address
  //   20-bit jump address
endmodule

module PC_control_unit (
  input  Branch,
  input  Jump,
  output [1:0] pc_controi_unit,
  output flush
);

  and and_1 (pc_controi_unit[1], ~Branch, Jump);  // AND_Gate
  or or_1 (flush, Branch, Jump);

  assign pc_controi_unit[0] = Branch;
endmodule

module Pipeline (
);

  wire alu_32_bit_1_p10, alu_32_bit_1_p15, alu_32_bit_1_p16, alucontrol_unit_1_p2, alucontrol_unit_1_p4,
       alucontrol_unit_1_p6, alucontrol_unit_1_p8, alucontrol_unit_1_p12, alucontrol_unit_1_p14, and_1_out,
       Branch, branch_control_unit_1_p2, branch_control_unit_1_p3, branch_control_unit_1_p4,
       branch_control_unit_1_p5, clock_1_out, jump, main_control_unit_1_p1, main_control_unit_1_p2,
       main_control_unit_1_p5, main_control_unit_1_p10, main_control_unit_1_p11, pc_control_unit_1_flush, R,
       sset, w;
  wire [4:0] IMM16, IMML, multiplexer_3_out, Rs1;
  wire [5:0] OP;
  wire [10:0] func;
  wire [19:0] next_pc_1_instruction_address, next_pc_1_pc_1;
  wire [31:0] alu_32_bit_1_p14, bit_extender_1_out, bit_extender_2_out, bit_extender_3_out,
       bit_extender_4_out, data_memory_1_p6, multiplexer_2_out, multiplexer_4_out, multiplexer_5_out,
       multiplexer_6_out, multiplexer_7_out, R1, R2, R3, R4, R5, R6, R7, R8, R9, R10, R11, R12, R13, R14,
       R15, R16, R17, R18, R19, R20, R21, R22, R23, R24, R25, R26, R27, R28, R29, R30, R31,
       register_file_1_read_data_1, register_file_1_read_data_2, rom_1_data;

  PC_control_unit pc_control_unit_1 (.flush(pc_control_unit_1_flush));  // open: Branch, Jump, pc_controi_unit
  ROM #(.addrWidth(20), .dataWidth(32)) rom_1 (.addr(next_pc_1_instruction_address), .data(rom_1_data));  // open: sel
  Multiplexer #(.width(32), .enable("false")) multiplexer_1 (
    .in0(rom_1_data), .in1({32{1'b0}}), .out({func, IMM16, Rs1, IMML, OP}), .sel(pc_control_unit_1_flush));
  // Main_Control_Unit main_control_unit_1: pin names not known; wires that end beside it: main_control_unit_1_p1, main_control_unit_1_p2, R, w, main_control_unit_1_p5, Branch, jump, Branch, sset, main_control_unit_1_p10, main_control_unit_1_p11
  // Probe on next_pc_1_instruction_address
  Clock clock_1 (.out(clock_1_out));
  Next_PC next_pc_1 (
    .ImmL_5(IMML), .ImmU_11(func), .Imm_16({func, IMM16}), .Rs1(register_file_1_read_data_1),
    .branch(and_1_out), .jump(jump), .PC_1(next_pc_1_pc_1),
    .Instruction_Address(next_pc_1_instruction_address), .Clock(clock_1_out));
  // Probe on R1
  assign bit_extender_1_out = {{12{1'b0}}, next_pc_1_pc_1};  // Bit_Extender bit_extender_1
  // Probe on R2
  // Probe on R3
  assign bit_extender_2_out = {{16{1'b0}}, {func, IMM16}};  // Bit_Extender bit_extender_2
  assign bit_extender_3_out = {{16{func[10]}}, {func, IMM16}};  // Bit_Extender bit_extender_3
  // Probe on R4
  assign bit_extender_4_out = {{16{func[10]}}, {func, IMML}};  // Bit_Extender bit_extender_4
  Multiplexer #(.width(32), .enable("false")) multiplexer_2 (
    .in0(bit_extender_2_out), .in1(bit_extender_3_out), .out(multiplexer_2_out), .sel(Branch));
  // Probe on R6
  // Probe on R5
  Multiplexer #(.width(5), .enable("false")) multiplexer_3 (.in0(Rs1), .in1(IMML), .out(multiplexer_3_out), .sel(sset));
  // Probe on R7
  // Probe on R8
  // Probe on R9
  // Probe on R10
  // Probe on R11
  // Probe on R12
  Register_File register_file_1 (
    .Write_data(multiplexer_7_out), .Read_Register_2(IMM16), .Read_Data_1(register_file_1_read_data_1),
    .Read_Data_2(register_file_1_read_data_2), .Read_Register_1(multiplexer_3_out), .Write_Register(IMML),
    .RegWrite(main_control_unit_1_p1), .Clock(clock_1_out), .R1(R1), .R2(R2), .R4(R4), .R3(R3), .R6(R6),
    .R5(R5), .R8(R8), .R7(R7), .R15(R15), .R14(R14), .R13(R13), .R12(R12), .R11(R11), .R10(R10), .R9(R9),
    .R16(R16), .R17(R17), .R18(R18), .R19(R19), .R20(R20), .R21(R21), .R22(R22), .R23(R23), .R24(R24),
    .R25(R25), .R26(R26), .R27(R27), .R28(R28), .R29(R29), .R30(R30), .R31(R31));
  // Probe on R14
  // Probe on R13
  // Probe on R15
  // Probe on R16
  // Probe on R17
  Multiplexer #(.width(32), .enable("false")) multiplexer_4 (
    .in0(register_file_1_read_data_2), .in1(multiplexer_2_out), .out(multiplexer_4_out),
    .sel(main_control_unit_1_p2));
  // Probe on R18
  // Probe on R19
  // Probe on R20
  // Probe on R22
  // Probe on R21
  Multiplexer #(.width(32), .enable("false")) multiplexer_5 (
    .in0(multiplexer_4_out), .in1(bit_extender_4_out), .out(multiplexer_5_out), .sel(main_control_unit_1_p11));
  // Probe on R23
  // ALUControl_Unit alucontrol_unit_1: pin names not known; wires that end beside it: clock_1_out, alucontrol_unit_1_p2, clock_1_out, alucontrol_unit_1_p4, clock_1_out, alucontrol_unit_1_p6, clock_1_out, alucontrol_unit_1_p8, clock_1_out, clock_1_out, clock_1_out, alucontrol_unit_1_p12, clock_1_out, alucontrol_unit_1_p14
  // Probe on R24
  // Probe on R25
  // Branch_control_unit branch_control_unit_1: pin names not known; wires that end beside it: OP, branch_control_unit_1_p2, branch_control_unit_1_p3, branch_control_unit_1_p4, branch_control_unit_1_p5
  // Probe on R26
  // Probe on R27
  // Probe on R28
  and and_1 (and_1_out, Branch, branch_control_unit_1_p5);
  // ALU_32_bit alu_32_bit_1: pin names not known; wires that end beside it: register_file_1_read_data_1, multiplexer_5_out, alucontrol_unit_1_p2, alucontrol_unit_1_p4, alucontrol_unit_1_p6, alucontrol_unit_1_p8, clock_1_out, alucontrol_unit_1_p14, alucontrol_unit_1_p12, alu_32_bit_1_p10, branch_control_unit_1_p2, branch_control_unit_1_p4, branch_control_unit_1_p3, alu_32_bit_1_p14, alu_32_bit_1_p15, alu_32_bit_1_p16
  // Probe on R30
  // Probe on R29
  // Probe on alu_32_bit_1_p15
  // Probe on alu_32_bit_1_p16
  // Probe on R31
  // Data_Memory data_memory_1: pin names not known; wires that end beside it: alu_32_bit_1_p14, register_file_1_read_data_2, w, clock_1_out, R, data_memory_1_p6
  Multiplexer #(.width(32), .enable("false")) multiplexer_6 (
    .in0(alu_32_bit_1_p14), .in1(data_memory_1_p6), .out(multiplexer_6_out), .sel(main_control_unit_1_p5));
  Multiplexer #(.width(32), .enable("false")) multiplexer_7 (
    .in0(multiplexer_6_out), .in1(bit_extender_1_out), .out(multiplexer_7_out), .sel(jump));

  // Other names for the same wires on the sheet: Rs2[4:0] = IMM16; Rd[4:0] = IMML; IMM16[15:5] = func;
  //   IMMU[10:0] = func

  // Notes on the sheet:
  //   contents of rom_1 (hex, n*v repeats v):
  //   1004d 10011 10051 a008d 20091 128900cd 45ac00ce 230711 500010d 7342010e 240751 384004d 1234020d
  //   5678020e 140945 12508c0 834100 50 10090 200d0 a42100 841100 c31180 30d2 820880 ffe00712 40011
  //   1a31280 245380 4453c0 57684 2501cf 4545024d 4545028d 95095 ffff0dcb 12 1431140 50 50890 608d0
  //   1631100 40011 380f
endmodule

module Hazard_Detect_Forward_and_Stall_Unit (
  input  [4:0] Rs,
  input  Reg_WR_EX,
  input  [4:0] Rd_EX,
  input  REG_WR_MEM,
  input  [4:0] Rd_MEM,
  input  REG_WR_WB,
  input  [4:0] Rd_WB,
  input  Mem_Read,
  input  [4:0] Rt,
  output [1:0] Forward_A,
  output Stall,
  output [1:0] Forward_B
);

  wire and_1_out, and_2_out, and_3_out, and_4_out, and_5_out, and_6_out, and_7_out, and_8_out,
       comparator_1_eq, comparator_2_eq, comparator_3_eq, comparator_4_eq, comparator_5_eq, comparator_6_eq,
       comparator_7_eq, comparator_8_eq, comparator_9_eq, comparator_10_eq, comparator_11_eq,
       comparator_12_eq, not_1_out, not_2_out, not_3_out, not_4_out, not_5_out, not_6_out, not_7_out,
       not_8_out, not_9_out, not_10_out, not_11_out, not_12_out, not_13_out, not_14_out, or_5_out;

  Comparator #(.width(5)) comparator_1 (.a({5{1'b0}}), .b(Rd_EX), .eq(comparator_1_eq));  // open: gt, lt
  Comparator #(.width(5)) comparator_2 (.a(Rd_EX), .b(Rs), .eq(comparator_2_eq));  // open: gt, lt
  Comparator #(.width(5)) comparator_3 (.a({5{1'b0}}), .b(Rd_MEM), .eq(comparator_3_eq));  // open: gt, lt
  Comparator #(.width(5)) comparator_4 (.a(Rd_MEM), .b(Rs), .eq(comparator_4_eq));  // open: gt, lt
  Comparator #(.width(5)) comparator_5 (.a({5{1'b0}}), .b(Rd_WB), .eq(comparator_5_eq));  // open: gt, lt
  Comparator #(.width(5)) comparator_6 (.a(Rd_WB), .b(Rs), .eq(comparator_6_eq));  // open: gt, lt
  Comparator #(.width(5)) comparator_7 (.a({5{1'b0}}), .b(Rd_EX), .eq(comparator_7_eq));  // open: gt, lt
  Comparator #(.width(5)) comparator_8 (.a(Rd_EX), .b(Rt), .eq(comparator_8_eq));  // open: gt, lt
  Comparator #(.width(5)) comparator_9 (.a({5{1'b0}}), .b(Rd_MEM), .eq(comparator_9_eq));  // open: gt, lt
  Comparator #(.width(5)) comparator_10 (.a(Rd_MEM), .b(Rt), .eq(comparator_10_eq));  // open: gt, lt
  Comparator #(.width(5)) comparator_11 (.a({5{1'b0}}), .b(Rd_WB), .eq(comparator_11_eq));  // open: gt, lt
  Comparator #(.width(5)) comparator_12 (.a(Rd_WB), .b(Rt), .eq(comparator_12_eq));  // open: gt, lt
  not not_1 (not_1_out, comparator_1_eq);
  and and_1 (and_1_out, Reg_WR_EX, not_1_out, comparator_2_eq);
  and and_2 (and_2_out, Reg_WR_EX, not_2_out, comparator_8_eq);
  not not_2 (not_2_out, comparator_7_eq);
  not not_3 (not_3_out, and_1_out);
  not not_4 (not_4_out, comparator_3_eq);
  not not_5 (not_5_out, and_2_out);
  and and_3 (and_3_out, not_3_out, REG_WR_MEM, not_4_out, comparator_4_eq);
  not not_6 (not_6_out, and_3_out);
  not not_7 (not_7_out, and_1_out);
  not not_8 (not_8_out, comparator_5_eq);
  and and_4 (and_4_out, not_5_out, REG_WR_MEM, not_9_out, comparator_10_eq);
  not not_9 (not_9_out, comparator_9_eq);
  and and_5 (and_5_out, not_6_out, REG_WR_WB, not_7_out, not_8_out, comparator_6_eq);
  not not_10 (not_10_out, and_2_out);
  not not_11 (not_11_out, and_4_out);
  not not_12 (not_12_out, comparator_11_eq);
  and and_6 (and_6_out, not_10_out, REG_WR_WB, not_11_out, not_12_out, comparator_12_eq);
  or or_1 (Forward_A[0], and_1_out, and_5_out);
  or or_2 (Forward_A[1], and_3_out, and_5_out);
  or or_3 (Forward_B[0], and_2_out, and_6_out);
  or or_4 (Forward_B[1], and_4_out, and_6_out);
  not not_13 (not_13_out, Forward_A[1]);
  not not_14 (not_14_out, Forward_B[1]);
  and and_7 (and_7_out, Forward_A[0], not_13_out);
  and and_8 (and_8_out, Forward_B[0], not_14_out);
  or or_5 (or_5_out, and_7_out, and_8_out);
  and and_9 (Stall, Mem_Read, or_5_out);
endmodule

module IM (
  input  [31:0] Instruction_Address
);


  // Other names for the same wires on the sheet: OP[5:0] = Instruction_Address[5:0];
  //   IMML[4:0] = Instruction_Address[10:6]; Rd[4:0] = Instruction_Address[10:6];
  //   Rs1[4:0] = Instruction_Address[15:11]; IMM16[15:0] = Instruction_Address[31:16];
  //   Rs2[4:0] = Instruction_Address[20:16]; func[10:0] = Instruction_Address[31:21];
  //   IMMU[10:0] = Instruction_Address[31:21]
endmodule

module PipelineProcessor (
  input  Clock
);

  wire Ainvert, alu_32_bit_1_carry_out, alu_32_bit_1_overflow, BCtrl, Binvert, Branch, BranchTaken, CarryIn,
       ExtOp, jump, LessF, LessUF, MemToReg, not_1_out, pc_control_unit_1_flush, R, R_En, RegWr, SLTCtrl,
       sset, Stall, SW, W, ZeroF, ZeroFlag;
  wire [0:0] ex_mem_1_control_signals_2;
  wire [1:0] alucontrol_unit_1_operation, alucontrol_unit_1_shftctrl, Fwd_A, Fwd_B, Operation,
       pc_control_unit_1_pc_controi_unit, ShftCtrl;
  wire [2:0] alucontrol_unit_1_resctrl, ResCtrl;
  wire [4:0] ex_mem_1_rd_2, id_ex_1_rd_2, IMM16, IMML, mem_wb_1_rd, multiplexer_3_out, RS1;
  wire [5:0] OP;
  wire [6:0] alucontrol_unit_1_carryin, main_control_unit_1_alusrc;
  wire [10:0] func;
  wire [16:12] id_ex_1_control_signals_2;
  wire [19:0] adder_1_out, ex_mem_1_alures_2, extender_1_branch_address, extender_1_jump_address,
       if_id_1_pc_1, multiplexer_1_out, multiplexer_8_out, PC_1, register_1_q;
  wire [31:0] ALUFwd, data_memory_1_out_6, ex_mem_1_b_2, extender_1_busb___immulextended, extender_1_imm16_2,
       id_ex_1_a_2, id_ex_1_b_2, id_ex_1_imm_2, MemFwd, multiplexer_2_out, multiplexer_4_out,
       multiplexer_5_out, multiplexer_6_out, multiplexer_7_out, R1, R2, R3, R4, R5, R6, R7, R8, R9, R10, R11,
       R12, R13, R14, R15, R16, R17, R18, R19, R20, R21, R22, R23, R24, R25, R26, R27, R28, R29, R30, R31,
       register_file_1_read_data_1, register_file_1_read_data_2, rom_1_data, WbFwd, WbFws;

  Multiplexer #(.select(2), .width(20), .enable("false")) multiplexer_1 (
    .in0(register_1_q), .in1(extender_1_branch_address), .in2(extender_1_jump_address),
    .out(multiplexer_1_out), .sel(pc_control_unit_1_pc_controi_unit));  // open: in3
  Register #(.width(20)) register_1 (.D(multiplexer_1_out), .en(not_1_out), .Q(register_1_q));  // open: clk, clr
  not not_1 (not_1_out, Stall);
  Adder #(.width(20)) adder_1 (.a(register_1_q), .b(20'h1), .out(adder_1_out), .cin(1'b0));  // open: cout
  ROM #(.addrWidth(20), .dataWidth(32)) rom_1 (.addr(register_1_q), .data(rom_1_data));  // open: sel
  PC_control_unit pc_control_unit_1 (
    .Branch(BranchTaken), .Jump(jump), .pc_controi_unit(pc_control_unit_1_pc_controi_unit),
    .flush(pc_control_unit_1_flush));
  Multiplexer #(.width(32), .enable("false")) multiplexer_2 (
    .in0(rom_1_data), .in1({32{1'b0}}), .out(multiplexer_2_out), .sel(pc_control_unit_1_flush));
  IF_ID if_id_1 (
    .PC__1(adder_1_out), .Instruction(multiplexer_2_out), .PC_1(if_id_1_pc_1),
    .Instruction_2({func, IMM16, RS1, IMML, OP}), .En(Stall), .Clock(Clock));
  Multiplexer #(.width(5), .enable("false")) multiplexer_3 (.in0(RS1), .in1(IMML), .out(multiplexer_3_out), .sel(sset));
  Register_File register_file_1 (
    .Write_data(WbFwd), .Read_Register_2(IMM16), .Read_Data_1(register_file_1_read_data_1),
    .Read_Data_2(register_file_1_read_data_2), .Read_Register_1(multiplexer_3_out), .Write_Register(IMML),
    .RegWrite(RegWr), .Clock(Clock), .R1(R1), .R2(R2), .R4(R4), .R3(R3), .R6(R6), .R5(R5), .R8(R8), .R7(R7),
    .R15(R15), .R14(R14), .R13(R13), .R12(R12), .R11(R11), .R10(R10), .R9(R9), .R16(R16), .R17(R17),
    .R18(R18), .R19(R19), .R20(R20), .R21(R21), .R22(R22), .R23(R23), .R24(R24), .R25(R25), .R26(R26),
    .R27(R27), .R28(R28), .R29(R29), .R30(R30), .R31(R31));
  Extender extender_1 (
    .PC(if_id_1_pc_1), .IMML(IMML), .IMMU(func), .IMM16({func, IMM16}), .Rs1(register_file_1_read_data_1),
    .Branch_Address(extender_1_branch_address), .BusB___immULExtended(extender_1_busb___immulextended),
    .Jump_Address(extender_1_jump_address), .IMM16_2(extender_1_imm16_2), .Clock(Clock), .ExtOp(ExtOp));
  Branch_control_unit branch_control_unit_1 (
    .in_1(OP), .zero_flag(ZeroF), .less_sign_flag(LessF), .less_unsign_flag(LessUF), .Branch(Branch),
    .BranchTaken(BranchTaken));
  ALUControl_Unit alucontrol_unit_1 (
    .Func(func), .OpCode(OP), .CarryIn(alucontrol_unit_1_carryin[0]), .Ainvert(alucontrol_unit_1_carryin[1]),
    .Binvert(alucontrol_unit_1_carryin[2]), .Operation(alucontrol_unit_1_operation),
    .SLTCtrl(alucontrol_unit_1_carryin[5]), .BranchCtrl(alucontrol_unit_1_carryin[6]),
    .ShftCtrl(alucontrol_unit_1_shftctrl), .ResCtrl(alucontrol_unit_1_resctrl), .Rtype_Enable(R_En));
  Hazard_Detect_Forward_and_Stall_Unit hazard_detect_forward_and_stall_unit_1 (
    .Reg_WR_EX(id_ex_1_control_signals_2[13]), .Rd_EX(id_ex_1_rd_2),
    .REG_WR_MEM(ex_mem_1_control_signals_2[0]), .Rd_MEM(ex_mem_1_rd_2), .REG_WR_WB(RegWr),
    .Rd_WB(mem_wb_1_rd), .Mem_Read(id_ex_1_control_signals_2[14]), .Forward_A(Fwd_A), .Stall(Stall),
    .Forward_B(Fwd_B), .Rs(RS1), .Rt(IMM16));
  Multiplexer #(.select(2), .width(32), .enable("false")) multiplexer_4 (
    .in0(register_file_1_read_data_1), .in1(ALUFwd), .in2(MemFwd), .in3(WbFws), .out(multiplexer_4_out),
    .sel(Fwd_A));
  Multiplexer #(.select(2), .width(32), .enable("false")) multiplexer_5 (
    .in0(register_file_1_read_data_2), .in1(ALUFwd), .in2(MemFwd), .in3(WbFws), .out(multiplexer_5_out),
    .sel(Fwd_B));
  Main_Control_Unit main_control_unit_1 (
    .RegWrite(main_control_unit_1_alusrc[1]), .ALUsrc(main_control_unit_1_alusrc[0]),
    .MemRead(main_control_unit_1_alusrc[2]), .MemWrite(main_control_unit_1_alusrc[3]),
    .MemToReg(main_control_unit_1_alusrc[4]), .ExtOp(ExtOp), .Branch(main_control_unit_1_alusrc[5]),
    .Jump(jump), .Opcode(OP), .R_TypeEnable(R_En), .SW(main_control_unit_1_alusrc[6]), .sset(sset));
  Comparator #(.width(32)) comparator_1 (.a(multiplexer_4_out), .b(multiplexer_5_out), .eq(ZeroF));  // open: gt, lt
  ID_EX id_ex_1 (
    .PC_1(register_1_q), .Rd(IMML), .IMM(extender_1_imm16_2), .A(multiplexer_4_out), .B(multiplexer_5_out),
    .Control_Signals({main_control_unit_1_alusrc, alucontrol_unit_1_resctrl, alucontrol_unit_1_shftctrl, alucontrol_unit_1_carryin[6:5], alucontrol_unit_1_operation, alucontrol_unit_1_carryin[2:0]}),
    .PC_1_2(PC_1), .Rd_2(id_ex_1_rd_2), .IMM_2(id_ex_1_imm_2), .A_2(id_ex_1_a_2), .B_2(id_ex_1_b_2),
    .Control_Signals_2({SW, Branch, id_ex_1_control_signals_2, ResCtrl, ShftCtrl, BCtrl, SLTCtrl, Operation, Binvert, Ainvert, CarryIn}),
    .Clock(Clock));
  Multiplexer #(.width(32), .enable("false")) multiplexer_6 (
    .in0(id_ex_1_b_2), .in1(id_ex_1_imm_2), .out(multiplexer_6_out), .sel(id_ex_1_control_signals_2[12]));
  Multiplexer #(.width(32), .enable("false")) multiplexer_7 (
    .in0(multiplexer_6_out), .in1(extender_1_busb___immulextended), .out(multiplexer_7_out), .sel(SW));
  ALU_32_bit alu_32_bit_1 (
    .A(id_ex_1_a_2), .B(multiplexer_7_out), .Binvert(Binvert), .Ainvert(Ainvert), .Operation(Operation),
    .ZeroFlag(ZeroFlag), .AluResult(ALUFwd), .Overflow(alu_32_bit_1_overflow), .Carry_In(CarryIn),
    .Carry_Out(alu_32_bit_1_carry_out), .ResCtrl(ResCtrl), .ShftCtrl(ShftCtrl), .BranchCtrl(BCtrl),
    .Less_sign_flag(LessF), .less_unsign_flag(LessUF), .SLTCtrl(SLTCtrl));
  // Probe on alu_32_bit_1_overflow
  // Probe on alu_32_bit_1_carry_out
  Multiplexer #(.width(20), .enable("false")) multiplexer_8 (
    .in0(ALUFwd[19:0]), .in1(PC_1), .out(multiplexer_8_out), .sel(jump));
  EX_MEM ex_mem_1 (
    .ALUres(multiplexer_8_out), .Rd(id_ex_1_rd_2), .B(id_ex_1_b_2),
    .Control_Signals(id_ex_1_control_signals_2[16:13]), .ALUres_2(ex_mem_1_alures_2), .Rd_2(ex_mem_1_rd_2),
    .B_2(ex_mem_1_b_2), .Control_Signals_2({MemToReg, W, R, ex_mem_1_control_signals_2[0]}), .Clock(Clock));
  Data_Memory data_memory_1 (
    .in_4(ex_mem_1_b_2), .in_2(W), .in_3(R), .out_6(data_memory_1_out_6), .in_5(ex_mem_1_alures_2));  // open: in_1
  Multiplexer #(.width(32), .enable("false")) multiplexer_9 (
    .in0(ALUFwd), .in1(data_memory_1_out_6), .out(MemFwd), .sel(MemToReg));
  MEM_WB mem_wb_1 (
    .DataOut(MemFwd), .in_2(ex_mem_1_rd_2), .RegWr(ex_mem_1_control_signals_2[0]), .DataOut_2(WbFwd),
    .Rd(mem_wb_1_rd), .RegWr_2(RegWr), .Clock(Clock));

  // Other names for the same wires on the sheet: Rd[4:0] = IMML; RS2[4:0] = IMM16; IMM16[15:5] = func;
  //   IMMU[10:0] = func
endmodule
