// Logisim project Project.circ as structural Verilog: 10 circuits, main circuit Next PC
module Register_File (
  input  [31:0] Write_data,
  input  [4:0] Read_Register_2,
  input  [4:0] Read_Register_1,
  input  [4:0] Write_Register,
  input  RegWrite,
  output [31:0] Read_Data_1,
  output [31:0] Read_Data_2
);

  wire and_2_out, and_3_out, and_4_out, and_5_out, and_6_out, and_7_out, and_8_out, and_9_out, and_10_out,
       and_11_out, and_12_out, and_13_out, and_14_out, and_15_out, and_16_out, and_17_out, and_18_out,
       and_19_out, and_20_out, and_21_out, and_22_out, and_23_out, and_24_out, and_25_out, and_26_out,
       and_27_out, and_28_out, and_29_out, and_30_out, and_31_out, and_32_out, clock_1_out, decoder_1_out0,
       decoder_1_out1, decoder_1_out2, decoder_1_out3, decoder_1_out4, decoder_1_out5, decoder_1_out6,
       decoder_1_out7, decoder_1_out8, decoder_1_out9, decoder_1_out10, decoder_1_out11, decoder_1_out12,
       decoder_1_out13, decoder_1_out14, decoder_1_out15, decoder_1_out16, decoder_1_out17, decoder_1_out18,
       decoder_1_out19, decoder_1_out20, decoder_1_out21, decoder_1_out22, decoder_1_out23, decoder_1_out24,
       decoder_1_out25, decoder_1_out26, decoder_1_out27, decoder_1_out28, decoder_1_out29, decoder_1_out30,
       decoder_1_out31;
  wire [31:0] register_1_q, register_2_q, register_3_q, register_4_q, register_5_q, register_6_q,
       register_7_q, register_8_q, register_9_q, register_10_q, register_11_q, register_12_q, register_13_q,
       register_14_q, register_15_q, register_16_q, register_17_q, register_18_q, register_19_q,
       register_20_q, register_21_q, register_22_q, register_23_q, register_24_q, register_25_q,
       register_26_q, register_27_q, register_28_q, register_29_q, register_30_q, register_31_q,
       register_32_q;

  Decoder #(.select(5), .enable("false")) decoder_1 (
    .out0(decoder_1_out0), .out1(decoder_1_out1), .out2(decoder_1_out2), .out3(decoder_1_out3),
    .out4(decoder_1_out4), .out5(decoder_1_out5), .out6(decoder_1_out6), .out7(decoder_1_out7),
    .out8(decoder_1_out8), .out9(decoder_1_out9), .out10(decoder_1_out10), .out11(decoder_1_out11),
    .out12(decoder_1_out12), .out13(decoder_1_out13), .out14(decoder_1_out14), .out15(decoder_1_out15),
    .out16(decoder_1_out16), .out17(decoder_1_out17), .out18(decoder_1_out18), .out19(decoder_1_out19),
    .out20(decoder_1_out20), .out21(decoder_1_out21), .out22(decoder_1_out22), .out23(decoder_1_out23),
    .out24(decoder_1_out24), .out25(decoder_1_out25), .out26(decoder_1_out26), .out27(decoder_1_out27),
    .out28(decoder_1_out28), .out29(decoder_1_out29), .out30(decoder_1_out30), .out31(decoder_1_out31),
    .sel(Write_Register));
  // AND_Gate and_1 has open pins: in0=decoder_1_out0, in1=RegWrite, out=open
  and and_2 (and_2_out, decoder_1_out1, RegWrite);
  and and_3 (and_3_out, decoder_1_out2, RegWrite);
  and and_4 (and_4_out, decoder_1_out3, RegWrite);
  and and_5 (and_5_out, decoder_1_out4, RegWrite);
  and and_6 (and_6_out, decoder_1_out5, RegWrite);
  and and_7 (and_7_out, decoder_1_out6, RegWrite);
  and and_8 (and_8_out, decoder_1_out7, RegWrite);
  and and_9 (and_9_out, decoder_1_out8, RegWrite);
  and and_10 (and_10_out, decoder_1_out9, RegWrite);
  and and_11 (and_11_out, decoder_1_out10, RegWrite);
  and and_12 (and_12_out, decoder_1_out11, RegWrite);
  and and_13 (and_13_out, decoder_1_out12, RegWrite);
  and and_14 (and_14_out, decoder_1_out13, RegWrite);
  and and_15 (and_15_out, decoder_1_out14, RegWrite);
  and and_16 (and_16_out, decoder_1_out15, RegWrite);
  and and_17 (and_17_out, decoder_1_out16, RegWrite);
  and and_18 (and_18_out, decoder_1_out17, RegWrite);
  and and_19 (and_19_out, decoder_1_out18, RegWrite);
  and and_20 (and_20_out, decoder_1_out19, RegWrite);
  and and_21 (and_21_out, decoder_1_out20, RegWrite);
  and and_22 (and_22_out, decoder_1_out21, RegWrite);
  and and_23 (and_23_out, decoder_1_out22, RegWrite);
  and and_24 (and_24_out, decoder_1_out23, RegWrite);
  and and_25 (and_25_out, decoder_1_out24, RegWrite);
  and and_26 (and_26_out, decoder_1_out25, RegWrite);
  and and_27 (and_27_out, decoder_1_out26, RegWrite);
  and and_28 (and_28_out, decoder_1_out27, RegWrite);
  and and_29 (and_29_out, decoder_1_out28, RegWrite);
  and and_30 (and_30_out, decoder_1_out29, RegWrite);
  and and_31 (and_31_out, decoder_1_out30, RegWrite);
  and and_32 (and_32_out, decoder_1_out31, RegWrite);
  Clock clock_1 (.out(clock_1_out));
  Register #(.width(32)) register_1 (.D({32{1'b0}}), .Q(register_1_q), .clk(clock_1_out));  // open: en, clr
  Register #(.width(32)) register_2 (.D(Write_data), .en(and_2_out), .Q(register_2_q), .clk(clock_1_out));  // open: clr
  Register #(.width(32)) register_3 (.D(Write_data), .en(and_3_out), .Q(register_3_q), .clk(clock_1_out));  // open: clr
  Register #(.width(32)) register_4 (.D(Write_data), .en(and_4_out), .Q(register_4_q), .clk(clock_1_out));  // open: clr
  Register #(.width(32)) register_5 (.D(Write_data), .en(and_5_out), .Q(register_5_q), .clk(clock_1_out));  // open: clr
  Register #(.width(32)) register_6 (.D(Write_data), .en(and_6_out), .Q(register_6_q), .clk(clock_1_out));  // open: clr
  Register #(.width(32)) register_7 (.D(Write_data), .en(and_7_out), .Q(register_7_q), .clk(clock_1_out));  // open: clr
  Register #(.width(32), .trigger("high")) register_8 (
    .D(Write_data), .en(and_8_out), .Q(register_8_q), .clk(clock_1_out));  // open: clr
  Register #(.width(32)) register_9 (.D(Write_data), .en(and_9_out), .Q(register_9_q), .clk(clock_1_out));  // open: clr
  Register #(.width(32)) register_10 (
    .D(Write_data), .en(and_10_out), .Q(register_10_q), .clk(clock_1_out));  // open: clr
  Register #(.width(32)) register_11 (
    .D(Write_data), .en(and_11_out), .Q(register_11_q), .clk(clock_1_out));  // open: clr
  Register #(.width(32)) register_12 (
    .D(Write_data), .en(and_12_out), .Q(register_12_q), .clk(clock_1_out));  // open: clr
  Register #(.width(32)) register_13 (
    .D(Write_data), .en(and_13_out), .Q(register_13_q), .clk(clock_1_out));  // open: clr
  Register #(.width(32)) register_14 (
    .D(Write_data), .en(and_14_out), .Q(register_14_q), .clk(clock_1_out));  // open: clr
  Register #(.width(32)) register_15 (
    .D(Write_data), .en(and_15_out), .Q(register_15_q), .clk(clock_1_out));  // open: clr
  Register #(.width(32)) register_16 (
    .D(Write_data), .en(and_16_out), .Q(register_16_q), .clk(clock_1_out));  // open: clr
  Register #(.width(32)) register_17 (
    .D(Write_data), .en(and_17_out), .Q(register_17_q), .clk(clock_1_out));  // open: clr
  Register #(.width(32)) register_18 (
    .D(Write_data), .en(and_18_out), .Q(register_18_q), .clk(clock_1_out));  // open: clr
  Register #(.width(32)) register_19 (
    .D(Write_data), .en(and_19_out), .Q(register_19_q), .clk(clock_1_out));  // open: clr
  Register #(.width(32)) register_20 (
    .D(Write_data), .en(and_20_out), .Q(register_20_q), .clk(clock_1_out));  // open: clr
  Register #(.width(32)) register_21 (
    .D(Write_data), .en(and_21_out), .Q(register_21_q), .clk(clock_1_out));  // open: clr
  Register #(.width(32)) register_22 (
    .D(Write_data), .en(and_22_out), .Q(register_22_q), .clk(clock_1_out));  // open: clr
  Register #(.width(32)) register_23 (
    .D(Write_data), .en(and_23_out), .Q(register_23_q), .clk(clock_1_out));  // open: clr
  Register #(.width(32)) register_24 (
    .D(Write_data), .en(and_24_out), .Q(register_24_q), .clk(clock_1_out));  // open: clr
  Register #(.width(32)) register_25 (
    .D(Write_data), .en(and_25_out), .Q(register_25_q), .clk(clock_1_out));  // open: clr
  Register #(.width(32)) register_26 (
    .D(Write_data), .en(and_26_out), .Q(register_26_q), .clk(clock_1_out));  // open: clr
  Register #(.width(32)) register_27 (
    .D(Write_data), .en(and_27_out), .Q(register_27_q), .clk(clock_1_out));  // open: clr
  Register #(.width(32)) register_28 (
    .D(Write_data), .en(and_28_out), .Q(register_28_q), .clk(clock_1_out));  // open: clr
  Register #(.width(32)) register_29 (
    .D(Write_data), .en(and_29_out), .Q(register_29_q), .clk(clock_1_out));  // open: clr
  Register #(.width(32)) register_30 (
    .D(Write_data), .en(and_30_out), .Q(register_30_q), .clk(clock_1_out));  // open: clr
  Register #(.width(32)) register_31 (
    .D(Write_data), .en(and_31_out), .Q(register_31_q), .clk(clock_1_out));  // open: clr
  Register #(.width(32)) register_32 (
    .D(Write_data), .en(and_32_out), .Q(register_32_q), .clk(clock_1_out));  // open: clr
  Multiplexer #(.select(5), .width(32), .enable("false")) multiplexer_1 (
    .in0(register_1_q), .in1(register_2_q), .in2(register_3_q), .in3(register_4_q), .in4(register_5_q),
    .in5(register_6_q), .in6(register_7_q), .in7(register_8_q), .in8(register_9_q), .in9(register_10_q),
    .in10(register_11_q), .in11(register_12_q), .in12(register_13_q), .in13(register_14_q),
    .in14(register_15_q), .in15(register_16_q), .in16(register_17_q), .in17(register_18_q),
    .in18(register_19_q), .in19(register_20_q), .in20(register_21_q), .in21(register_22_q),
    .in22(register_23_q), .in23(register_24_q), .in24(register_25_q), .in25(register_26_q),
    .in26(register_27_q), .in27(register_28_q), .in28(register_29_q), .in29(register_30_q),
    .in30(register_31_q), .in31(register_32_q), .out(Read_Data_1), .sel(Read_Register_1));
  Multiplexer #(.select(5), .width(32), .enable("false")) multiplexer_2 (
    .in0(register_1_q), .in1(register_2_q), .in2(register_3_q), .in3(register_4_q), .in4(register_5_q),
    .in5(register_6_q), .in6(register_7_q), .in7(register_8_q), .in8(register_9_q), .in9(register_10_q),
    .in10(register_11_q), .in11(register_12_q), .in12(register_13_q), .in13(register_14_q),
    .in14(register_15_q), .in15(register_16_q), .in16(register_17_q), .in17(register_18_q),
    .in18(register_19_q), .in19(register_20_q), .in20(register_21_q), .in21(register_22_q),
    .in22(register_23_q), .in23(register_24_q), .in24(register_25_q), .in25(register_26_q),
    .in26(register_27_q), .in27(register_28_q), .in28(register_29_q), .in29(register_30_q),
    .in30(register_31_q), .in31(register_32_q), .out(Read_Data_2), .sel(Read_Register_2));

  // Notes on the sheet:
  //   Clock
endmodule

module ALU_32_bit (
  input  [31:0] A,
  input  [31:0] B,
  input  Carry_In,
  input  Ainvert,
  input  Binvert,
  input  [1:0] Operation,
  input  [2:0] ResCtrl,
  input  [1:0] ShftCtrl,
  input  BranchCtrl,
  output ZeroFlag,
  output [31:0] AluResult,
  output Overflow,
  output Less_sign_flag,
  output Carry_Out,
  output less_unsign_flag
);

  wire alu_1_bit_1_carry_out, alu_1_bit_2_carry_out, alu_1_bit_3_carry_out, alu_1_bit_4_carry_out,
       alu_1_bit_5_carry_out, alu_1_bit_6_carry_out, alu_1_bit_7_carry_out, alu_1_bit_8_carry_out,
       alu_1_bit_9_carry_out, alu_1_bit_10_carry_out, alu_1_bit_11_carry_out, alu_1_bit_12_carry_out,
       alu_1_bit_13_carry_out, alu_1_bit_14_carry_out, alu_1_bit_15_carry_out, alu_1_bit_16_carry_out,
       alu_1_bit_17_carry_out, alu_1_bit_18_carry_out, alu_1_bit_19_carry_out, alu_1_bit_20_carry_out,
       alu_1_bit_21_carry_out, alu_1_bit_22_carry_out, alu_1_bit_23_carry_out, alu_1_bit_24_carry_out,
       alu_1_bit_25_carry_out, alu_1_bit_26_carry_out, alu_1_bit_27_carry_out, alu_1_bit_28_carry_out,
       alu_1_bit_29_carry_out, alu_1_bit_30_carry_out, alu_1_bit_31_carry_out, and_1_out, and_2_out,
       and_3_out, comparator_1_eq, comparator_1_gt, comparator_2_eq, comparator_2_gt, comparator_3_eq,
       comparator_3_gt, comparator_3_lt, not_2_out, not_3_out, not_4_out, not_5_out, not_6_out, not_7_out,
       or_1_out, R0, R1, R2, R3, R4, R5, R6, R7, R8, R9, R10, R11, R12, R13, R14, R15, R16, R17, R18, R19,
       R20, R21, R22, R23, R24, R25, R26, R27, R28, R29, R30, R31;
  wire [30:0] multiplier_1_out;
  wire [31:0] adder_1_out, adder_2_out, bit_extender_1_out, bit_extender_2_out, bit_extender_3_out,
       bit_extender_4_out, bit_extender_5_out, multiplexer_1_out, multiplexer_2_out, shifter_1_out,
       shifter_2_out, shifter_3_out, shifter_4_out, shifter_5_out;
  wire [31:31] xor_2_out;

  ALU_1_bit alu_1_bit_1 (
    .A(A[0]), .B(B[0]), .Carry_In(Carry_In), .Result(R0), .Carry_Out(alu_1_bit_1_carry_out),
    .Ainvert(Ainvert), .Binvert(Binvert), .Operation(Operation));
  ALU_1_bit alu_1_bit_2 (
    .A(A[1]), .B(B[1]), .Carry_In(alu_1_bit_1_carry_out), .Result(R1), .Carry_Out(alu_1_bit_2_carry_out),
    .Ainvert(Ainvert), .Binvert(Binvert), .Operation(Operation));
  ALU_1_bit alu_1_bit_3 (
    .A(A[2]), .B(B[2]), .Carry_In(alu_1_bit_2_carry_out), .Result(R2), .Carry_Out(alu_1_bit_3_carry_out),
    .Ainvert(Ainvert), .Binvert(Binvert), .Operation(Operation));
  ALU_1_bit alu_1_bit_4 (
    .A(A[3]), .B(B[3]), .Carry_In(alu_1_bit_3_carry_out), .Result(R3), .Carry_Out(alu_1_bit_4_carry_out),
    .Ainvert(Ainvert), .Binvert(Binvert), .Operation(Operation));
  ALU_1_bit alu_1_bit_5 (
    .A(A[4]), .B(B[4]), .Carry_In(alu_1_bit_4_carry_out), .Result(R4), .Carry_Out(alu_1_bit_5_carry_out),
    .Ainvert(Ainvert), .Binvert(Binvert), .Operation(Operation));
  ALU_1_bit alu_1_bit_6 (
    .A(A[5]), .B(B[5]), .Carry_In(alu_1_bit_5_carry_out), .Result(R5), .Carry_Out(alu_1_bit_6_carry_out),
    .Ainvert(Ainvert), .Binvert(Binvert), .Operation(Operation));
  ALU_1_bit alu_1_bit_7 (
    .A(A[6]), .B(B[6]), .Carry_In(alu_1_bit_6_carry_out), .Result(R6), .Carry_Out(alu_1_bit_7_carry_out),
    .Ainvert(Ainvert), .Binvert(Binvert), .Operation(Operation));
  ALU_1_bit alu_1_bit_8 (
    .A(A[7]), .B(B[7]), .Carry_In(alu_1_bit_7_carry_out), .Result(R7), .Carry_Out(alu_1_bit_8_carry_out),
    .Ainvert(Ainvert), .Binvert(Binvert), .Operation(Operation));
  ALU_1_bit alu_1_bit_9 (
    .A(A[8]), .B(B[8]), .Carry_In(alu_1_bit_8_carry_out), .Result(R8), .Carry_Out(alu_1_bit_9_carry_out),
    .Ainvert(Ainvert), .Binvert(Binvert), .Operation(Operation));
  ALU_1_bit alu_1_bit_10 (
    .A(A[9]), .B(B[9]), .Carry_In(alu_1_bit_9_carry_out), .Result(R9), .Carry_Out(alu_1_bit_10_carry_out),
    .Ainvert(Ainvert), .Binvert(Binvert), .Operation(Operation));
  ALU_1_bit alu_1_bit_11 (
    .A(A[10]), .B(B[10]), .Carry_In(alu_1_bit_10_carry_out), .Result(R10),
    .Carry_Out(alu_1_bit_11_carry_out), .Ainvert(Ainvert), .Binvert(Binvert), .Operation(Operation));
  ALU_1_bit alu_1_bit_12 (
    .A(A[11]), .B(B[11]), .Carry_In(alu_1_bit_11_carry_out), .Result(R11),
    .Carry_Out(alu_1_bit_12_carry_out), .Ainvert(Ainvert), .Binvert(Binvert), .Operation(Operation));
  ALU_1_bit alu_1_bit_13 (
    .A(A[12]), .B(B[12]), .Carry_In(alu_1_bit_12_carry_out), .Result(R12),
    .Carry_Out(alu_1_bit_13_carry_out), .Ainvert(Ainvert), .Binvert(Binvert), .Operation(Operation));
  ALU_1_bit alu_1_bit_14 (
    .A(A[13]), .B(B[13]), .Carry_In(alu_1_bit_13_carry_out), .Result(R13),
    .Carry_Out(alu_1_bit_14_carry_out), .Ainvert(Ainvert), .Binvert(Binvert), .Operation(Operation));
  ALU_1_bit alu_1_bit_15 (
    .A(A[14]), .B(B[14]), .Carry_In(alu_1_bit_14_carry_out), .Result(R14),
    .Carry_Out(alu_1_bit_15_carry_out), .Ainvert(Ainvert), .Binvert(Binvert), .Operation(Operation));
  ALU_1_bit alu_1_bit_16 (
    .A(A[15]), .B(B[15]), .Carry_In(alu_1_bit_15_carry_out), .Result(R15),
    .Carry_Out(alu_1_bit_16_carry_out), .Ainvert(Ainvert), .Binvert(Binvert), .Operation(Operation));
  ALU_1_bit alu_1_bit_17 (
    .A(A[16]), .B(B[16]), .Carry_In(alu_1_bit_16_carry_out), .Result(R16),
    .Carry_Out(alu_1_bit_17_carry_out), .Ainvert(Ainvert), .Binvert(Binvert), .Operation(Operation));
  ALU_1_bit alu_1_bit_18 (
    .A(A[17]), .B(B[17]), .Carry_In(alu_1_bit_17_carry_out), .Result(R17),
    .Carry_Out(alu_1_bit_18_carry_out), .Ainvert(Ainvert), .Binvert(Binvert), .Operation(Operation));
  ALU_1_bit alu_1_bit_19 (
    .A(A[18]), .B(B[18]), .Carry_In(alu_1_bit_18_carry_out), .Result(R18),
    .Carry_Out(alu_1_bit_19_carry_out), .Ainvert(Ainvert), .Binvert(Binvert), .Operation(Operation));
  ALU_1_bit alu_1_bit_20 (
    .A(A[19]), .B(B[19]), .Carry_In(alu_1_bit_19_carry_out), .Result(R19),
    .Carry_Out(alu_1_bit_20_carry_out), .Ainvert(Ainvert), .Binvert(Binvert), .Operation(Operation));
  ALU_1_bit alu_1_bit_21 (
    .A(A[20]), .B(B[20]), .Carry_In(alu_1_bit_20_carry_out), .Result(R20),
    .Carry_Out(alu_1_bit_21_carry_out), .Ainvert(Ainvert), .Binvert(Binvert), .Operation(Operation));
  ALU_1_bit alu_1_bit_22 (
    .A(A[21]), .B(B[21]), .Carry_In(alu_1_bit_21_carry_out), .Result(R21),
    .Carry_Out(alu_1_bit_22_carry_out), .Ainvert(Ainvert), .Binvert(Binvert), .Operation(Operation));
  ALU_1_bit alu_1_bit_23 (
    .A(A[22]), .B(B[22]), .Carry_In(alu_1_bit_22_carry_out), .Result(R22),
    .Carry_Out(alu_1_bit_23_carry_out), .Ainvert(Ainvert), .Binvert(Binvert), .Operation(Operation));
  ALU_1_bit alu_1_bit_24 (
    .A(A[23]), .B(B[23]), .Carry_In(alu_1_bit_23_carry_out), .Result(R23),
    .Carry_Out(alu_1_bit_24_carry_out), .Ainvert(Ainvert), .Binvert(Binvert), .Operation(Operation));
  ALU_1_bit alu_1_bit_25 (
    .A(A[24]), .B(B[24]), .Carry_In(alu_1_bit_24_carry_out), .Result(R24),
    .Carry_Out(alu_1_bit_25_carry_out), .Ainvert(Ainvert), .Binvert(Binvert), .Operation(Operation));
  ALU_1_bit alu_1_bit_26 (
    .A(A[25]), .B(B[25]), .Carry_In(alu_1_bit_25_carry_out), .Result(R25),
    .Carry_Out(alu_1_bit_26_carry_out), .Ainvert(Ainvert), .Binvert(Binvert), .Operation(Operation));
  ALU_1_bit alu_1_bit_27 (
    .A(A[26]), .B(B[26]), .Carry_In(alu_1_bit_26_carry_out), .Result(R26),
    .Carry_Out(alu_1_bit_27_carry_out), .Ainvert(Ainvert), .Binvert(Binvert), .Operation(Operation));
  ALU_1_bit alu_1_bit_28 (
    .A(A[27]), .B(B[27]), .Carry_In(alu_1_bit_27_carry_out), .Result(R27),
    .Carry_Out(alu_1_bit_28_carry_out), .Ainvert(Ainvert), .Binvert(Binvert), .Operation(Operation));
  ALU_1_bit alu_1_bit_29 (
    .A(A[28]), .B(B[28]), .Carry_In(alu_1_bit_28_carry_out), .Result(R28),
    .Carry_Out(alu_1_bit_29_carry_out), .Ainvert(Ainvert), .Binvert(Binvert), .Operation(Operation));
  ALU_1_bit alu_1_bit_30 (
    .A(A[29]), .B(B[29]), .Carry_In(alu_1_bit_29_carry_out), .Result(R29),
    .Carry_Out(alu_1_bit_30_carry_out), .Ainvert(Ainvert), .Binvert(Binvert), .Operation(Operation));
  ALU_1_bit alu_1_bit_31 (
    .A(A[30]), .B(B[30]), .Carry_In(alu_1_bit_30_carry_out), .Result(R30),
    .Carry_Out(alu_1_bit_31_carry_out), .Ainvert(Ainvert), .Binvert(Binvert), .Operation(Operation));
  ALU_1_bit alu_1_bit_32 (
    .A(A[31]), .B(B[31]), .Carry_In(alu_1_bit_31_carry_out), .Result(R31), .Carry_Out(Carry_Out),
    .Ainvert(Ainvert), .Binvert(Binvert), .Operation(Operation));
  xor xor_1 (Overflow, alu_1_bit_31_carry_out, Carry_Out);
  or or_1 (or_1_out, R0, R1, R2, R3, R4, R5, R6, R7, R8, R9, R10, R11, R12, R13, R14, R15, R16, R17, R18, R19, R20, R21, R22, R23, R24, R25, R26, R27, R28, R29, R30, R31);
  not not_1 (ZeroFlag, or_1_out);
  Shifter #(.width(32)) shifter_1 (.in(A), .\dist (5'b10000), .out(shifter_1_out));
  assign bit_extender_1_out = {{16{1'b0}}, B[15:0]};  // Bit_Extender bit_extender_1
  Shifter #(.width(32)) shifter_2 (.in(A), .\dist (B[4:0]), .out(shifter_2_out));
  Shifter #(.width(32), .shift("lr")) shifter_3 (.in(A), .\dist (B[4:0]), .out(shifter_3_out));
  Shifter #(.width(32), .shift("ar")) shifter_4 (.in(A), .\dist (B[4:0]), .out(shifter_4_out));
  Shifter #(.width(32), .shift("rr")) shifter_5 (.in(A), .\dist (B[4:0]), .out(shifter_5_out));
  Comparator #(.width(32)) comparator_1 (.a(A), .b(B), .gt(comparator_1_gt), .eq(comparator_1_eq), .lt(Less_sign_flag));
  Comparator #(.width(32), .mode("unsigned")) comparator_2 (
    .a(A), .b(B), .gt(comparator_2_gt), .eq(comparator_2_eq), .lt(less_unsign_flag));
  Comparator #(.width(32), .mode("unsigned")) comparator_3 (
    .a(A), .b(B), .gt(comparator_3_gt), .eq(comparator_3_eq), .lt(comparator_3_lt));
  not not_2 (not_2_out, comparator_1_gt);
  and and_1 (and_1_out, not_2_out, not_3_out, Less_sign_flag);
  not not_3 (not_3_out, comparator_1_eq);
  not not_4 (not_4_out, comparator_2_gt);
  not not_5 (not_5_out, comparator_2_eq);
  and and_2 (and_2_out, not_4_out, not_5_out, less_unsign_flag);
  not not_6 (not_6_out, comparator_3_gt);
  not not_7 (not_7_out, comparator_3_lt);
  assign bit_extender_2_out = {{31{1'b0}}, and_1_out};  // Bit_Extender bit_extender_2
  assign bit_extender_3_out = {{31{1'b0}}, and_2_out};  // Bit_Extender bit_extender_3
  and and_3 (and_3_out, not_6_out, comparator_3_eq, not_7_out);
  assign bit_extender_4_out = {{31{1'b0}}, and_3_out};  // Bit_Extender bit_extender_4
  assign bit_extender_5_out = {{31{1'b0}}, R31};  // Bit_Extender bit_extender_5
  Multiplier #(.width(31)) multiplier_1 (.a(A[30:0]), .b(B[30:0]), .out(multiplier_1_out));  // open: cin, cout
  xor xor_2 (xor_2_out[31], A[31], B[31]);
  Adder #(.width(32)) adder_1 (.a(B), .b({32{1'b0}}), .out(adder_1_out), .cin(1'b0));  // open: cout
  Adder #(.width(32)) adder_2 (.a(shifter_1_out), .b(bit_extender_1_out), .out(adder_2_out), .cin(1'b0));  // open: cout
  Multiplexer #(.select(2), .width(32), .enable("false")) multiplexer_1 (
    .in0(shifter_2_out), .in1(shifter_3_out), .in2(shifter_4_out), .in3(shifter_5_out),
    .out(multiplexer_1_out), .sel(ShftCtrl));
  Multiplexer #(.width(32), .enable("false")) multiplexer_2 (
    .in0(bit_extender_2_out), .in1(bit_extender_3_out), .out(multiplexer_2_out), .sel(BranchCtrl));
  Multiplexer #(.select(3), .width(32), .enable("false")) multiplexer_3 (
    .in0({R31, R30, R29, R28, R27, R26, R25, R24, R23, R22, R21, R20, R19, R18, R17, R16, R15, R14, R13, R12, R11, R10, R9, R8, R7, R6, R5, R4, R3, R2, R1, R0}),
    .in1(multiplexer_1_out), .in2(multiplexer_2_out), .in3(bit_extender_4_out), .in4(bit_extender_5_out),
    .in5({xor_2_out[31], multiplier_1_out}), .in6(adder_1_out), .in7(adder_2_out), .out(AluResult),
    .sel(ResCtrl));

  // Other names for the same wires on the sheet: b_t[4:0] = B[4:0]

  // Notes on the sheet:
  //   SLL
  //   SRL
  //   SRA
  //   ROR
  //   BEQ / BNE
  //   BEQ / BNE
  //   SEQ
  //   SLT
  //   MUL
  //   SET
  //   SSET
  //   Signed
  //   Unsigned
endmodule

module Next_PC (
  input  [4:0] ImmL_5,
  input  [10:0] ImmU_11,
  input  [15:0] Imm_16,
  input  jump,
  input  branch,
  input  [31:0] Rs1_Test_Input,
  output [19:0] PC_1,
  output [19:0] PC
);

  wire clock_1_out;
  wire [19:0] adder_2_out, adder_3_out, bit_extender_1_out, multiplexer_1_out, PC_t;
  wire [31:0] bit_extender_2_out, Rs1_q;
  wire [31:20] adder_3_out_2;

  Clock clock_1 (.out(clock_1_out));
  Register #(.width(20)) u_PC (.D(PC), .Q(PC_t), .clk(clock_1_out));  // open: en, clr
  Adder #(.width(20)) adder_1 (.a(PC_t), .b(20'h1), .out(PC_1));  // open: cin, cout
  // Probe on PC_1
  assign bit_extender_1_out = {{4{1'b0}}, {ImmU_11, ImmL_5}};  // Bit_Extender bit_extender_1
  assign bit_extender_2_out = {{16{1'b0}}, Imm_16};  // Bit_Extender bit_extender_2
  Register #(.width(32)) Rs1 (.D(Rs1_Test_Input), .Q(Rs1_q), .clk(clock_1_out));  // open: en, clr
  Adder #(.width(20)) adder_2 (.a(PC_1), .b(bit_extender_1_out), .out(adder_2_out), .cin(1'b0));  // open: cout
  Adder #(.width(32)) adder_3 (
    .a(bit_extender_2_out), .b(Rs1_q), .out({adder_3_out_2, adder_3_out}), .cin(1'b0));  // open: cout
  // Probe on adder_2_out
  // Probe on adder_3_out
  Multiplexer #(.width(20), .enable("false")) multiplexer_1 (
    .in0(PC_1), .in1(adder_2_out), .out(multiplexer_1_out), .sel(branch));
  Multiplexer #(.width(20), .enable("false")) multiplexer_2 (
    .in0(adder_3_out), .in1(multiplexer_1_out), .out(PC), .sel(jump));

  // Notes on the sheet:
  //   PC + 1
  //   PC + 1
endmodule

module ALU_1_bit (
  input  A,
  input  Ainvert,
  input  B,
  input  Binvert,
  input  [1:0] Operation,
  input  Carry_In,
  output Result,
  output Carry_Out
);

  wire adder_1_out, and_1_out, multiplexer_1_out, multiplexer_2_out, not_1_out, not_2_out, or_1_out,
       xor_1_out;

  Multiplexer #(.enable("false")) multiplexer_1 (.in0(A), .in1(not_1_out), .out(multiplexer_1_out), .sel(Ainvert));
  not not_1 (not_1_out, A);
  Multiplexer #(.enable("false")) multiplexer_2 (.in0(B), .in1(not_2_out), .out(multiplexer_2_out), .sel(Binvert));
  not not_2 (not_2_out, B);
  and and_1 (and_1_out, multiplexer_1_out, multiplexer_2_out);
  or or_1 (or_1_out, multiplexer_1_out, multiplexer_2_out);
  xor xor_1 (xor_1_out, multiplexer_1_out, multiplexer_2_out);
  Adder #(.width(1)) adder_1 (
    .a(multiplexer_1_out), .b(multiplexer_2_out), .out(adder_1_out), .cin(Carry_In), .cout(Carry_Out));
  Multiplexer #(.select(2), .enable("false")) multiplexer_3 (
    .in0(and_1_out), .in1(or_1_out), .in2(xor_1_out), .in3(adder_1_out), .out(Result), .sel(Operation));
endmodule

module Main_Control_Unit (
  input  [31:0] Opcode,
  output RegDst,
  output RegWrite,
  output ALUsrc,
  output MemRead,
  output MemWrite,
  output MemToReg,
  output Branch,
  output Jump,
  output ExtOp,
  output ALUctrl1,
  output ALUctrl0
);

  wire and_1_out, and_2_out, and_4_out, and_5_out, and_6_out, and_7_out, and_8_out, and_9_out, and_10_out,
       and_11_out, and_12_out, and_13_out, and_16_out, and_17_out, and_18_out, and_19_out, and_20_out,
       and_21_out, and_22_out, and_23_out, and_24_out, and_25_out, and_26_out, and_27_out, not_1_out,
       not_2_out, not_3_out, not_4_out, not_5_out, not_6_out, not_7_out, not_8_out, not_9_out, not_10_out,
       not_11_out, not_12_out, not_13_out, not_14_out, not_15_out, not_16_out, not_17_out, not_18_out,
       not_19_out, not_20_out, not_21_out, not_22_out, not_23_out, not_24_out, not_25_out, not_26_out,
       not_27_out, not_28_out, not_29_out, not_30_out, not_31_out, not_32_out, not_33_out, not_34_out,
       not_35_out, not_36_out, not_37_out, not_38_out;

  not not_1 (not_1_out, Opcode[30]);
  not not_2 (not_2_out, Opcode[29]);
  not not_3 (not_3_out, Opcode[28]);
  not not_4 (not_4_out, Opcode[27]);
  not not_5 (not_5_out, Opcode[26]);
  not not_6 (not_6_out, Opcode[28]);
  not not_7 (not_7_out, Opcode[27]);
  not not_8 (not_8_out, Opcode[26]);
  not not_9 (not_9_out, Opcode[30]);
  not not_10 (not_10_out, Opcode[29]);
  not not_11 (not_11_out, Opcode[30]);
  not not_12 (not_12_out, Opcode[29]);
  not not_13 (not_13_out, Opcode[30]);
  not not_14 (not_14_out, Opcode[29]);
  not not_15 (not_15_out, Opcode[28]);
  not not_16 (not_16_out, Opcode[27]);
  not not_17 (not_17_out, Opcode[26]);
  not not_18 (not_18_out, Opcode[28]);
  not not_19 (not_19_out, Opcode[27]);
  not not_20 (not_20_out, Opcode[28]);
  not not_21 (not_21_out, Opcode[27]);
  not not_22 (not_22_out, Opcode[26]);
  not not_23 (not_23_out, Opcode[28]);
  not not_24 (not_24_out, Opcode[27]);
  not not_25 (not_25_out, Opcode[26]);
  and and_1 (and_1_out, Opcode[30], Opcode[27]);
  and and_2 (and_2_out, Opcode[30], Opcode[28]);
  and and_3 (Jump, Opcode[29], Opcode[28], Opcode[27], Opcode[26]);
  not not_26 (not_26_out, Opcode[28]);
  not not_27 (not_27_out, Opcode[27]);
  not not_28 (not_28_out, Opcode[26]);
  not not_29 (not_29_out, Opcode[27]);
  not not_30 (not_30_out, Opcode[26]);
  not not_31 (not_31_out, Opcode[30]);
  not not_32 (not_32_out, Opcode[29]);
  not not_33 (not_33_out, Opcode[28]);
  not not_34 (not_34_out, Opcode[27]);
  not not_35 (not_35_out, Opcode[26]);
  not not_36 (not_36_out, Opcode[26]);
  not not_37 (not_37_out, Opcode[26]);
  and and_4 (and_4_out, not_1_out, not_2_out, not_3_out, not_4_out, not_5_out);
  and and_5 (and_5_out, Opcode[29], Opcode[28], Opcode[27], Opcode[26]);
  not not_38 (not_38_out, Opcode[30]);
  and and_6 (and_6_out, not_6_out, not_7_out, not_8_out);
  and and_7 (and_7_out, not_9_out, not_10_out, Opcode[26]);
  and and_8 (and_8_out, not_11_out, not_12_out, Opcode[27]);
  and and_9 (and_9_out, not_13_out, not_14_out, Opcode[28]);
  and and_10 (and_10_out, Opcode[29], not_15_out);
  and and_11 (and_11_out, Opcode[29], not_16_out);
  and and_12 (and_12_out, Opcode[29], not_17_out);
  and and_13 (and_13_out, Opcode[30], not_18_out, not_19_out);
  and and_14 (MemRead, Opcode[30], not_20_out, not_21_out, not_22_out);
  and and_15 (MemWrite, Opcode[30], not_23_out, not_24_out, Opcode[26]);
  and and_16 (and_16_out, Opcode[30], not_25_out);
  and and_17 (and_17_out, Opcode[30], Opcode[27]);
  or or_1 (Branch, and_1_out, and_2_out);
  and and_18 (and_18_out, not_26_out, not_27_out, not_28_out);
  and and_19 (and_19_out, Opcode[28], not_29_out, Opcode[26]);
  and and_20 (and_20_out, Opcode[28], Opcode[27], not_30_out);
  and and_21 (and_21_out, Opcode[29], Opcode[28], Opcode[27]);
  and and_22 (and_22_out, not_31_out, not_32_out, not_33_out, not_34_out, not_35_out);
  and and_23 (and_23_out, Opcode[29], Opcode[28], Opcode[27], not_36_out);
  and and_24 (and_24_out, Opcode[29], Opcode[28], Opcode[27], not_37_out);
  and and_25 (and_25_out, Opcode[30], Opcode[26]);
  and and_26 (and_26_out, Opcode[30], Opcode[27]);
  and and_27 (and_27_out, Opcode[30], Opcode[28]);
  or or_2 (RegDst, and_4_out, and_5_out);
  or or_3 (RegWrite, not_38_out, and_6_out);
  or or_4 (ALUsrc, and_7_out, and_8_out, and_9_out, and_10_out, and_11_out, and_12_out, and_13_out);
  or or_5 (MemToReg, and_16_out, and_17_out);
  or or_6 (ExtOp, and_18_out, and_19_out, and_20_out, and_21_out, Opcode[30]);
  or or_7 (ALUctrl1, and_22_out, and_23_out);
  or or_8 (ALUctrl0, and_24_out, and_25_out, and_26_out, and_27_out);
endmodule

module ALU_Control_Unit (
  input  [5:0] ALUOpcode,
  input  [10:0] Func,
  output CarryIn,
  output Ainvert,
  output Binvert,
  output [1:0] Operation,
  output [1:0] ShiftCtrl,
  output BranchCtrl,
  output [2:0] ResCtrl
);

  wire and_1_out, and_2_out, and_3_out, and_4_out, and_5_out, and_6_out, and_7_out, and_8_out, and_9_out,
       and_10_out, and_11_out, and_12_out, and_13_out, and_14_out, and_15_out, and_16_out, and_17_out,
       and_18_out, and_19_out, and_20_out, and_21_out, and_22_out, and_23_out, and_24_out, and_25_out,
       and_26_out, and_27_out, and_28_out, and_29_out, and_30_out, and_31_out, and_32_out, and_33_out,
       and_34_out, and_35_out, and_36_out, and_37_out, and_38_out, and_39_out, and_40_out, and_41_out,
       and_42_out, and_43_out, and_44_out, and_45_out, and_46_out, and_47_out, and_48_out, and_49_out,
       and_50_out, and_51_out, and_52_out, and_53_out, not_1_out, not_2_out, not_3_out, not_4_out, not_5_out,
       not_6_out, not_7_out, not_8_out, not_9_out, not_10_out, not_11_out, not_12_out, not_13_out,
       not_14_out, not_15_out, not_16_out, not_17_out, not_18_out, not_19_out, not_20_out, not_21_out,
       not_22_out, not_23_out, not_24_out, not_25_out, not_26_out, not_27_out, not_28_out, not_29_out,
       not_30_out, not_31_out, not_32_out, not_33_out, not_34_out, not_35_out, not_36_out, not_37_out,
       not_38_out, not_39_out, not_40_out, not_41_out, not_42_out, not_43_out, not_44_out, not_45_out,
       not_46_out, not_47_out, not_48_out, not_49_out, not_50_out, not_51_out, not_52_out, not_53_out,
       not_54_out, not_55_out, not_56_out, not_57_out, not_58_out, not_59_out, not_60_out, not_61_out,
       not_62_out, not_63_out, not_64_out, not_65_out, not_66_out, not_67_out, not_68_out, not_69_out,
       not_70_out, not_71_out, not_72_out, not_73_out, not_74_out, not_75_out, not_76_out, not_77_out,
       not_78_out, not_79_out, not_80_out, not_81_out, not_82_out, not_83_out, not_84_out;

  not not_1 (not_1_out, Func[3]);
  not not_2 (not_2_out, Func[2]);
  not not_3 (not_3_out, Func[1]);
  not not_4 (not_4_out, Func[0]);
  not not_5 (not_5_out, ALUOpcode[3]);
  not not_6 (not_6_out, ALUOpcode[3]);
  not not_7 (not_7_out, ALUOpcode[2]);
  not not_8 (not_8_out, ALUOpcode[1]);
  not not_9 (not_9_out, ALUOpcode[0]);
  not not_10 (not_10_out, Func[0]);
  not not_11 (not_11_out, ALUOpcode[1]);
  not not_12 (not_12_out, ALUOpcode[0]);
  not not_13 (not_13_out, Func[3]);
  not not_14 (not_14_out, Func[1]);
  not not_15 (not_15_out, Func[0]);
  not not_16 (not_16_out, ALUOpcode[3]);
  not not_17 (not_17_out, ALUOpcode[1]);
  not not_18 (not_18_out, ALUOpcode[0]);
  not not_19 (not_19_out, Func[3]);
  not not_20 (not_20_out, Func[2]);
  not not_21 (not_21_out, Func[1]);
  not not_22 (not_22_out, ALUOpcode[3]);
  not not_23 (not_23_out, ALUOpcode[3]);
  not not_24 (not_24_out, ALUOpcode[2]);
  not not_25 (not_25_out, ALUOpcode[1]);
  not not_26 (not_26_out, Func[3]);
  not not_27 (not_27_out, Func[2]);
  not not_28 (not_28_out, Func[0]);
  not not_29 (not_29_out, ALUOpcode[3]);
  not not_30 (not_30_out, ALUOpcode[3]);
  not not_31 (not_31_out, ALUOpcode[2]);
  not not_32 (not_32_out, ALUOpcode[0]);
  not not_33 (not_33_out, Func[3]);
  not not_34 (not_34_out, Func[2]);
  not not_35 (not_35_out, ALUOpcode[4]);
  not not_36 (not_36_out, ALUOpcode[3]);
  not not_37 (not_37_out, ALUOpcode[2]);
  not not_38 (not_38_out, ALUOpcode[4]);
  not not_39 (not_39_out, ALUOpcode[3]);
  not not_40 (not_40_out, ALUOpcode[1]);
  not not_41 (not_41_out, ALUOpcode[0]);
  not not_42 (not_42_out, Func[3]);
  not not_43 (not_43_out, Func[2]);
  not not_44 (not_44_out, ALUOpcode[4]);
  not not_45 (not_45_out, ALUOpcode[3]);
  not not_46 (not_46_out, ALUOpcode[2]);
  not not_47 (not_47_out, ALUOpcode[0]);
  not not_48 (not_48_out, ALUOpcode[4]);
  not not_49 (not_49_out, ALUOpcode[3]);
  not not_50 (not_50_out, ALUOpcode[1]);
  not not_51 (not_51_out, ALUOpcode[0]);
  not not_52 (not_52_out, ALUOpcode[4]);
  not not_53 (not_53_out, ALUOpcode[3]);
  not not_54 (not_54_out, ALUOpcode[0]);
  not not_55 (not_55_out, ALUOpcode[1]);
  not not_56 (not_56_out, ALUOpcode[4]);
  not not_57 (not_57_out, ALUOpcode[3]);
  not not_58 (not_58_out, ALUOpcode[4]);
  not not_59 (not_59_out, ALUOpcode[0]);
  not not_60 (not_60_out, ALUOpcode[1]);
  not not_61 (not_61_out, Func[2]);
  not not_62 (not_62_out, Func[1]);
  not not_63 (not_63_out, Func[0]);
  not not_64 (not_64_out, ALUOpcode[2]);
  not not_65 (not_65_out, ALUOpcode[1]);
  not not_66 (not_66_out, ALUOpcode[0]);
  not not_67 (not_67_out, ALUOpcode[1]);
  not not_68 (not_68_out, ALUOpcode[0]);
  not not_69 (not_69_out, ALUOpcode[4]);
  not not_70 (not_70_out, ALUOpcode[3]);
  not not_71 (not_71_out, ALUOpcode[2]);
  not not_72 (not_72_out, Func[3]);
  not not_73 (not_73_out, Func[2]);
  not not_74 (not_74_out, ALUOpcode[4]);
  not not_75 (not_75_out, ALUOpcode[3]);
  not not_76 (not_76_out, ALUOpcode[1]);
  not not_77 (not_77_out, ALUOpcode[0]);
  not not_78 (not_78_out, Func[2]);
  not not_79 (not_79_out, Func[1]);
  not not_80 (not_80_out, Func[0]);
  not not_81 (not_81_out, ALUOpcode[2]);
  not not_82 (not_82_out, ALUOpcode[1]);
  not not_83 (not_83_out, ALUOpcode[0]);
  not not_84 (not_84_out, ALUOpcode[0]);
  and and_1 (and_1_out, not_1_out, Func[2]);
  and and_2 (and_2_out, Func[3], not_2_out, not_3_out, not_4_out);
  and and_3 (and_3_out, not_5_out, ALUOpcode[2], ALUOpcode[0]);
  and and_4 (and_4_out, not_6_out, ALUOpcode[2], ALUOpcode[1]);
  and and_5 (and_5_out, ALUOpcode[2], ALUOpcode[1], ALUOpcode[0]);
  and and_6 (and_6_out, ALUOpcode[3], not_7_out, not_8_out, not_9_out);
  and and_7 (and_7_out, Func[3], Func[2], not_10_out);
  and and_8 (and_8_out, ALUOpcode[3], ALUOpcode[2], not_11_out, not_12_out);
  and and_9 (and_9_out, not_13_out, Func[2], Func[0]);
  and and_10 (and_10_out, Func[2], Func[1]);
  and and_11 (and_11_out, Func[3], not_14_out, not_15_out);
  and and_12 (and_12_out, not_16_out, ALUOpcode[2], ALUOpcode[1]);
  and and_13 (and_13_out, ALUOpcode[3], not_17_out, not_18_out);
  and and_14 (and_14_out, ALUOpcode[4], ALUOpcode[1]);
  and and_15 (and_15_out, ALUOpcode[4], ALUOpcode[2]);
  and and_16 (and_16_out, not_19_out, Func[2]);
  and and_17 (and_17_out, Func[2], Func[0]);
  and and_18 (and_18_out, Func[3], not_20_out, not_21_out);
  and and_19 (and_19_out, not_22_out, ALUOpcode[2], ALUOpcode[0]);
  and and_20 (and_20_out, not_23_out, ALUOpcode[2], ALUOpcode[1]);
  and and_21 (and_21_out, ALUOpcode[2], ALUOpcode[1], ALUOpcode[0]);
  and and_22 (and_22_out, ALUOpcode[3], not_24_out, not_25_out);
  and and_23 (and_23_out, not_26_out, Func[2]);
  and and_24 (and_24_out, Func[2], Func[0]);
  and and_25 (and_25_out, Func[3], not_27_out, not_28_out);
  and and_26 (and_26_out, not_29_out, ALUOpcode[2], ALUOpcode[0]);
  and and_27 (and_27_out, not_30_out, ALUOpcode[2], ALUOpcode[1]);
  and and_28 (and_28_out, ALUOpcode[2], ALUOpcode[1], ALUOpcode[0]);
  and and_29 (and_29_out, ALUOpcode[3], not_31_out, not_32_out);
  and and_30 (and_30_out, not_33_out, not_34_out, Func[1]);
  and and_31 (and_31_out, not_35_out, not_36_out, not_37_out, ALUOpcode[1], ALUOpcode[0]);
  and and_32 (and_32_out, not_38_out, not_39_out, ALUOpcode[2], not_40_out, not_41_out);
  and and_33 (and_33_out, not_42_out, not_43_out, Func[0]);
  and and_34 (and_34_out, not_44_out, not_45_out, not_46_out, ALUOpcode[1], not_47_out);
  and and_35 (and_35_out, not_48_out, not_49_out, ALUOpcode[2], not_50_out, not_51_out);
  and and_36 (and_36_out, not_52_out, not_53_out, ALUOpcode[2], ALUOpcode[1], not_54_out);
  and and_37 (and_37_out, ALUOpcode[4], ALUOpcode[2], not_55_out);
  and and_38 (and_38_out, Func[2], Func[1]);
  and and_39 (and_39_out, Func[3], Func[2], Func[0]);
  and and_40 (and_40_out, not_56_out, not_57_out, ALUOpcode[2], ALUOpcode[1]);
  and and_41 (and_41_out, not_58_out, ALUOpcode[2], ALUOpcode[1], not_59_out);
  and and_42 (and_42_out, ALUOpcode[3], ALUOpcode[2], not_60_out, ALUOpcode[0]);
  and and_43 (and_43_out, Func[3], not_61_out, not_62_out, not_63_out);
  and and_44 (and_44_out, ALUOpcode[3], not_64_out, not_65_out, not_66_out);
  and and_45 (and_45_out, ALUOpcode[3], ALUOpcode[2], not_67_out, ALUOpcode[0]);
  and and_46 (and_46_out, ALUOpcode[3], ALUOpcode[2], ALUOpcode[1], not_68_out);
  and and_47 (and_47_out, ALUOpcode[4], ALUOpcode[1]);
  and and_48 (and_48_out, ALUOpcode[4], ALUOpcode[2]);
  and and_49 (and_49_out, not_69_out, not_70_out, not_71_out, not_72_out, not_73_out);
  and and_50 (and_50_out, not_74_out, not_75_out, not_76_out, not_77_out, not_78_out, not_79_out, not_80_out);
  and and_51 (and_51_out, Func[3], Func[2], Func[0]);
  and and_52 (and_52_out, ALUOpcode[3], not_81_out, not_82_out, not_83_out);
  and and_53 (and_53_out, ALUOpcode[3], ALUOpcode[2], ALUOpcode[1], not_84_out);
  or or_1 (CarryIn, and_1_out, and_2_out, and_3_out, and_4_out, and_5_out, and_6_out, ALUOpcode[4]);
  or or_2 (Ainvert, and_7_out, and_8_out);
  or or_3 (Binvert, and_9_out, and_10_out, and_11_out, and_12_out, and_13_out, and_14_out, and_15_out);
  or or_4 (Operation[1], and_16_out, and_17_out, and_18_out, and_19_out, and_20_out, and_21_out, and_22_out, ALUOpcode[4]);
  or or_5 (Operation[0], and_23_out, and_24_out, and_25_out, and_26_out, and_27_out, and_28_out, and_29_out, ALUOpcode[4]);
  or or_6 (ShiftCtrl[1], and_30_out, and_31_out, and_32_out);
  or or_7 (ShiftCtrl[0], and_33_out, and_34_out, and_35_out);
  or or_8 (BranchCtrl, and_36_out, and_37_out);
  or or_9 (ResCtrl[2], and_38_out, and_39_out, and_40_out, and_41_out, and_42_out);
  or or_10 (ResCtrl[1], and_43_out, and_44_out, and_45_out, and_46_out, and_47_out, and_48_out);
  or or_11 (ResCtrl[0], and_49_out, and_50_out, and_51_out, and_52_out, and_53_out);
endmodule

module Full_Processor (
);

  wire alu_32_bit_1_less_sign_flag, alu_32_bit_1_less_unsign_flag, alu_32_bit_1_zeroflag,
       alu_control_unit_1_ainvert, alu_control_unit_1_binvert, alu_control_unit_1_branchctrl,
       alu_control_unit_1_carryin, and_1_out, Branch, branch_control_unit_1_branch, clock_1_out, jump,
       main_control_unit_1_alusrc, main_control_unit_1_extop, main_control_unit_1_regdst,
       main_control_unit_1_regwrite, memory_to_reg, R, undriven, w;
  wire [1:0] alu_control_unit_1_operation, alu_control_unit_1_shiftctrl;
  wire [2:0] alu_control_unit_1_resctrl;
  wire [4:0] IMML, multiplexer_2_out;
  wire [5:0] OP, op_t;
  wire [15:0] IMM16;
  wire [15:11] rom_1_data;
  wire [19:0] next_pc_1_pc_1, PC;
  wire [31:0] alu_32_bit_1_aluresult, bit_extender_1_out, bit_extender_2_out, bit_extender_3_out,
       data_memory_1_out_6, multiplexer_1_out, multiplexer_3_out, multiplexer_4_out, multiplexer_5_out,
       register_file_1_read_data_1, register_file_1_read_data_2;

  Clock clock_1 (.out(clock_1_out));
  ROM #(.addrWidth(20), .dataWidth(32)) rom_1 (.addr(PC), .data({IMM16, rom_1_data, IMML, OP}));  // open: sel
  assign bit_extender_1_out = {{16{1'b0}}, IMM16};  // Bit_Extender bit_extender_1
  assign bit_extender_2_out = {{16{IMM16[15]}}, IMM16};  // Bit_Extender bit_extender_2
  Main_Control_Unit main_control_unit_1 (
    .Opcode({IMM16, rom_1_data, IMML, OP}), .RegDst(main_control_unit_1_regdst),
    .RegWrite(main_control_unit_1_regwrite), .ALUsrc(main_control_unit_1_alusrc), .MemRead(R), .MemWrite(w),
    .MemToReg(memory_to_reg), .ExtOp(main_control_unit_1_extop), .Branch(Branch), .Jump(jump));  // open: ALUctrl1, ALUctrl0
  Next_PC next_pc_1 (
    .ImmL_5(IMML), .ImmU_11(IMM16[15:5]), .Imm_16(IMM16), .Rs1_Test_Input(register_file_1_read_data_1),
    .branch(and_1_out), .jump(jump), .PC(PC), .PC_1(next_pc_1_pc_1));
  Multiplexer #(.width(32), .enable("false")) multiplexer_1 (
    .in0(bit_extender_1_out), .in1(bit_extender_2_out), .out(multiplexer_1_out),
    .sel(main_control_unit_1_extop));
  assign bit_extender_3_out = {{12{1'b0}}, next_pc_1_pc_1};  // Bit_Extender bit_extender_3
  Multiplexer #(.width(5), .enable("false")) multiplexer_2 (
    .in0(IMM16[4:0]), .in1(IMML), .out(multiplexer_2_out), .sel(main_control_unit_1_regdst));
  Register_File register_file_1 (
    .Write_data(multiplexer_5_out), .Read_Register_2(IMM16[4:0]), .Read_Data_1(register_file_1_read_data_1),
    .Read_Data_2(register_file_1_read_data_2), .Read_Register_1(rom_1_data),
    .Write_Register(multiplexer_2_out), .RegWrite(main_control_unit_1_regwrite));
  Multiplexer #(.width(32), .enable("false")) multiplexer_3 (
    .in0(register_file_1_read_data_2), .in1(multiplexer_1_out), .out(multiplexer_3_out),
    .sel(main_control_unit_1_alusrc));
  Branch_control_unit branch_control_unit_1 (
    .in_1(op_t), .zero_flag(alu_32_bit_1_zeroflag), .less_sign_flag(alu_32_bit_1_less_sign_flag),
    .less_unsign_flag(alu_32_bit_1_less_unsign_flag), .Branch(branch_control_unit_1_branch));
  ALU_Control_Unit alu_control_unit_1 (
    .ALUOpcode(OP), .Func(IMM16[15:5]), .CarryIn(alu_control_unit_1_carryin),
    .Ainvert(alu_control_unit_1_ainvert), .Binvert(alu_control_unit_1_binvert),
    .Operation(alu_control_unit_1_operation), .ShiftCtrl(alu_control_unit_1_shiftctrl),
    .BranchCtrl(alu_control_unit_1_branchctrl), .ResCtrl(alu_control_unit_1_resctrl));
  and and_1 (and_1_out, Branch, branch_control_unit_1_branch);
  ALU_32_bit alu_32_bit_1 (
    .A(register_file_1_read_data_1), .B(multiplexer_3_out), .Binvert(alu_control_unit_1_binvert),
    .Ainvert(alu_control_unit_1_ainvert), .Operation(alu_control_unit_1_operation),
    .ZeroFlag(alu_32_bit_1_zeroflag), .AluResult(alu_32_bit_1_aluresult),
    .Carry_In(alu_control_unit_1_carryin), .ResCtrl(alu_control_unit_1_resctrl),
    .ShftCtrl(alu_control_unit_1_shiftctrl), .BranchCtrl(alu_control_unit_1_branchctrl),
    .Less_sign_flag(alu_32_bit_1_less_sign_flag), .less_unsign_flag(alu_32_bit_1_less_unsign_flag));  // open: Overflow, Carry_Out
  Data_Memory data_memory_1 (
    .out_6(data_memory_1_out_6), .in_4(register_file_1_read_data_2), .in_5(alu_32_bit_1_aluresult), .in_2(w),
    .in_3(R), .in_1(undriven));
  Multiplexer #(.width(32), .enable("false")) multiplexer_4 (
    .in0(alu_32_bit_1_aluresult), .in1(data_memory_1_out_6), .out(multiplexer_4_out), .sel(memory_to_reg));
  Multiplexer #(.width(32), .enable("false")) multiplexer_5 (
    .in0(multiplexer_4_out), .in1(bit_extender_3_out), .out(multiplexer_5_out), .sel(jump));

  // Other names for the same wires on the sheet: Rd[4:0] = IMML; IMMU[10:0] = IMM16[15:5]

  // Notes on the sheet:
  //   contents of rom_1 (hex, n*v repeats v):
  //   11111111 11111111 1111 1 12*0 1111
endmodule

module Instruction_Memory (
  input  [19:0] in_1,
  output [5:0] out_2,
  output [4:0] out_3,
  output [4:0] out_4,
  output [4:0] out_5,
  output [10:0] out_6,
  output [15:0] out_7
);

  ROM #(.addrWidth(20), .dataWidth(32)) rom_1 (.addr(in_1), .data({out_6, out_5, out_4, out_3, out_2}));  // open: sel

  assign out_7 = {out_6, out_5};

  // Other names for the same wires on the sheet: OP[5:0] = out_2; IMML[4:0] = out_3; Rd[4:0] = out_3; Rs[4:0] = out_4;
  //   IMM16[15:0] = {out_6, out_5}; Rt[4:0] = out_5; IMMU[10:0] = out_6; PC[19:0] = in_1

  // Notes on the sheet:
  //   contents of rom_1 (hex, n*v repeats v):
  //   1004d 10011 10051 a008d 20091 128900cd 45ac00ce 230711 500010d 7342010e 240751 384004d 1234020d
  //   5678020e 140945 12508c0 834100 50 10090 200d0 a42100 841100 c31180 30d2 820880 ffe00712 40011
  //   1a31280 245380 4453c0 57684 2501cf 4545024d 4545028d 95095 ffff0dcb 12 1431140 50 50890 608d0
  //   1631100 40011 380f
endmodule

module Data_Memory (
  input  in_1,
  input  in_2,
  input  in_3,
  input  [31:0] in_4,
  input  [31:0] in_5,
  output [31:0] out_6
);

  RAM #(.addrWidth(20), .dataWidth(32), .bus("separate")) ram_1 (
    .addr(in_5[19:0]), .din(in_4), .data(out_6), .str(in_2), .clk(in_1), .ld(in_3));  // open: sel, clr

  // Other names for the same wires on the sheet: AluResuit[31:0] = in_5; BusB[31:0] = in_4; Memory_Read = in_3;
  //   Memory_Write = in_2
endmodule

module Branch_control_unit (
  input  [5:0] in_1,
  input  zero_flag,
  input  less_sign_flag,
  input  less_unsign_flag,
  output Branch
);

  wire and_1_out, and_2_out, and_3_out, and_4_out, and_5_out, and_6_out, not_1_out, not_2_out, not_3_out,
       not_4_out, not_5_out, not_6_out, not_7_out, not_8_out, not_9_out, not_10_out, not_11_out, not_12_out,
       not_13_out, not_14_out, not_15_out, not_16_out;

  not not_1 (not_1_out, in_1[0]);
  not not_2 (not_2_out, in_1[2]);
  not not_3 (not_3_out, in_1[3]);
  not not_4 (not_4_out, in_1[2]);
  not not_5 (not_5_out, in_1[3]);
  not not_6 (not_6_out, zero_flag);
  not not_7 (not_7_out, in_1[0]);
  not not_8 (not_8_out, in_1[1]);
  not not_9 (not_9_out, in_1[3]);
  not not_10 (not_10_out, in_1[1]);
  not not_11 (not_11_out, in_1[3]);
  not not_12 (not_12_out, less_sign_flag);
  not not_13 (not_13_out, in_1[0]);
  not not_14 (not_14_out, in_1[3]);
  not not_15 (not_15_out, in_1[3]);
  not not_16 (not_16_out, less_unsign_flag);
  and and_1 (and_1_out, not_1_out, in_1[1], not_2_out, not_3_out, in_1[4], zero_flag);
  and and_2 (and_2_out, in_1[0], in_1[1], not_4_out, not_5_out, in_1[4], not_6_out);
  and and_3 (and_3_out, not_7_out, not_8_out, in_1[2], not_9_out, in_1[4], less_sign_flag);
  and and_4 (and_4_out, in_1[0], not_10_out, in_1[2], not_11_out, in_1[4], not_12_out);
  and and_5 (and_5_out, not_13_out, in_1[1], in_1[2], not_14_out, in_1[4], less_unsign_flag);
  and and_6 (and_6_out, in_1[0], in_1[1], in_1[2], not_15_out, in_1[4], not_16_out);
  or or_1 (Branch, and_1_out, and_2_out, and_3_out, and_4_out, and_5_out, and_6_out);

  // Notes on the sheet:
  //   opcode
  //   BEQ
  //   BNE
  //   BLT
  //   BGT
  //   BLTU
  //   BGTU
endmodule
